// Logisim project 2-1-MUX-hazard电路.circ as structural Verilog: 4 circuits, main circuit main
module main (
  input  D0,
  input  D1,
  input  S,
  output out_4
);

  wire and_1_out, and_2_out, not_1_out;

  // Probe on S
  not not_1 (not_1_out, S);
  // Probe on not_1_out
  and and_1 (and_1_out, D0, not_1_out);
  and and_2 (and_2_out, D1, S);
  \or  or_1 (.in_1(and_1_out), .in_2(and_2_out), .out_3(out_4));
endmodule

module \or  (
  input  in_1,
  input  in_2,
  output out_3
);

  wire transistor_1_out, transistor_2_out;

  Transistor transistor_1 (.in(1'b1), .out(transistor_1_out), .gate(in_1));
  Transistor transistor_2 (.in(transistor_1_out), .out(transistor_2_out), .gate(in_2));
  Transistor #(.\type ("n")) transistor_3 (.in(1'b0), .out(transistor_2_out), .gate(in_1));
  Transistor #(.\type ("n")) transistor_4 (.in(1'b0), .out(transistor_2_out), .gate(in_2));
  Transistor transistor_5 (.in(1'b1), .out(out_3), .gate(transistor_2_out));
  Transistor #(.\type ("n")) transistor_6 (.in(1'b0), .out(out_3), .gate(transistor_2_out));
endmodule

module _4_1_MUX (
  input  D0,
  input  D1,
  input  D2,
  input  D3,
  input  S0,
  input  S1,
  output out_7
);

  wire main_1_out_4, main_2_out_4;

  main main_1 (.D0(D0), .D1(D1), .S(S0), .out_4(main_1_out_4));
  main main_2 (.D0(D2), .D1(D3), .S(S0), .out_4(main_2_out_4));
  main main_3 (.D0(main_1_out_4), .D1(main_2_out_4), .S(S1), .out_4(out_7));
endmodule

module XOR (
  input  N0,
  input  N1,
  input  N2,
  input  N3,
  output EVEN,
  output ODD
);

  wire xor_1_out, xor_2_out;

  xor xor_1 (xor_1_out, N0, N1);
  xor xor_2 (xor_2_out, N2, N3);
  xor xor_3 (EVEN, xor_1_out, xor_2_out);
  not not_1 (ODD, EVEN);
endmodule
