// Logisim project 实验1.circ as structural Verilog: 5 circuits, main circuit main
module main (
  input  X,
  input  Y,
  input  Z,
  output F
);

  wire and_1_out, and_2_out, and_3_out;

  and and_1 (and_1_out, X, Z);
  and and_2 (and_2_out, Y, X);
  and and_3 (and_3_out, Z, Y);
  or or_1 (F, and_1_out, and_2_out, and_3_out);
endmodule

module _12 (
  input  X,
  input  Y,
  output Z
);

  wire transistor_1_out, transistor_2_out;

  Transistor transistor_1 (.in(1'b1), .out(transistor_1_out), .gate(X));
  Transistor transistor_2 (.in(transistor_1_out), .out(transistor_2_out), .gate(Y));
  Transistor #(.\type ("n")) transistor_3 (.in(1'b0), .out(transistor_2_out), .gate(X));
  Transistor #(.\type ("n")) transistor_4 (.in(1'b0), .out(transistor_2_out), .gate(Y));
  Transistor transistor_5 (.in(1'b1), .out(Z), .gate(transistor_2_out));
  Transistor #(.\type ("n")) transistor_6 (.in(1'b0), .out(Z), .gate(transistor_2_out));
endmodule

module _13 (
  input  D0,
  input  D1,
  input  S,
  output Y
);

  wire and_1_out, and_2_out, not_1_out;

  not not_1 (not_1_out, S);
  and and_1 (and_1_out, D0, not_1_out);
  and and_2 (and_2_out, D1, S);
  or or_1 (Y, and_1_out, and_2_out);
endmodule

module _14 (
  input  D1,
  input  D0,
  input  S,
  output Y
);

  wire transistor_1_out;

  Transistor transistor_1 (.in(1'b1), .out(transistor_1_out), .gate(S));
  Transistor #(.\type ("n")) transistor_2 (.in(1'b0), .out(transistor_1_out), .gate(S));
  // Transmission_Gate transmission_1: pin names not known; wires that end beside it: D1, S, transistor_1_out, Y
  // Transmission_Gate transmission_2: pin names not known; wires that end beside it: D0, transistor_1_out, S, Y
endmodule

// D0
module _15 (
  input  D0,
  input  D1,
  input  D2,
  input  D3,
  input  S0,
  input  S1,
  output Y
);

  wire n13_1_y, n13_2_y;

  _13 u_13_1 (.D0(D0), .D1(D1), .S(S0), .Y(n13_1_y));
  _13 u_13_2 (.D0(D2), .D1(D3), .S(S0), .Y(n13_2_y));
  _13 u_13_3 (.D0(n13_1_y), .D1(n13_2_y), .S(S1), .Y(Y));
endmodule
