// Logisim project 实验一思考题2.circ as structural Verilog: 7 circuits, main circuit 4-1-MUX
module main (
  input  D0,
  input  D1,
  input  S,
  output Y
);

  wire and_1_out, and_2_out, not_1_out;

  // Probe on S
  not not_1 (not_1_out, S);
  // Probe on not_1_out
  and and_1 (and_1_out, D0, not_1_out);
  and and_2 (and_2_out, D1, S);
  \or  or_1 (.in_1(and_1_out), .in_2(and_2_out), .out_3(Y));
endmodule

module \or  (
  input  in_1,
  input  in_2,
  output out_3
);

  wire transistor_1_out, transistor_2_out;

  Transistor transistor_1 (.in(1'b1), .out(transistor_1_out), .gate(in_1));
  Transistor transistor_2 (.in(transistor_1_out), .out(transistor_2_out), .gate(in_2));
  Transistor #(.\type ("n")) transistor_3 (.in(1'b0), .out(transistor_2_out), .gate(in_1));
  Transistor #(.\type ("n")) transistor_4 (.in(1'b0), .out(transistor_2_out), .gate(in_2));
  Transistor transistor_5 (.in(1'b1), .out(out_3), .gate(transistor_2_out));
  Transistor #(.\type ("n")) transistor_6 (.in(1'b0), .out(out_3), .gate(transistor_2_out));
endmodule

module _4_1_MUX (
  input  [15:0] INPUT,
  input  [1:0] SELECT,
  output [3:0] OUTPUT
);

  wire [3:0] n4_4_1_out_4, n4_4_2_out_4;

  _4_4 u_4_4_1 (.in_1(INPUT[3:0]), .in_2(INPUT[7:4]), .in_3(SELECT[0]), .out_4(n4_4_1_out_4));
  _4_4 u_4_4_2 (.in_1(INPUT[11:8]), .in_2(INPUT[15:12]), .in_3(SELECT[0]), .out_4(n4_4_2_out_4));
  _4_4 u_4_4_3 (.in_1(n4_4_1_out_4), .in_2(n4_4_2_out_4), .in_3(SELECT[1]), .out_4(OUTPUT));

  // Other names for the same wires on the sheet: DATA[15:0] = INPUT; S[1:0] = SELECT; Y[3:0] = OUTPUT
endmodule

module XOR (
  input  N0,
  input  N1,
  input  N2,
  input  N3,
  output EVEN,
  output ODD
);

  wire xor_1_out, xor_2_out;

  xor xor_1 (xor_1_out, N0, N1);
  xor xor_2 (xor_2_out, N2, N3);
  xor xor_3 (EVEN, xor_1_out, xor_2_out);
  not not_1 (ODD, EVEN);
endmodule

module \new  (
  input  [3:0] in_1,
  input  [3:0] in_2,
  output [3:0] out_3
);

  wire [3:0] and_1_out, and_2_out, not_1_out;

  assign not_1_out = ~in_2;  // NOT_Gate not_1, 4 bits wide
  assign and_1_out = in_1 & not_1_out;  // AND_Gate and_1, 4 bits wide
  assign and_2_out = in_1 & in_2;  // AND_Gate and_2, 4 bits wide
  assign out_3 = and_1_out | and_2_out;  // OR_Gate or_1, 4 bits wide

  // Other names for the same wires on the sheet: input[3:0] = in_1; S[3:0] = in_2
endmodule

module _4_1 (
  input  in_1,
  input  in_2,
  input  in_3,
  input  in_4,
  input  in_5,
  input  in_6,
  output out_7
);

  wire main_1_y, main_2_y;

  main main_1 (.D0(in_1), .D1(in_1), .S(in_5), .Y(main_1_y));
  main main_2 (.D0(in_3), .D1(in_4), .S(in_5), .Y(main_2_y));
  main main_3 (.D0(main_1_y), .D1(main_2_y), .S(in_6), .Y(out_7));

  assign in_2 = in_1;
endmodule

module _4_4 (
  input  [3:0] in_1,
  input  [3:0] in_2,
  input  in_3,
  output [3:0] out_4
);

  Multiplexer #(.enable("false")) multiplexer_1 (.in0(in_1[0]), .in1(in_2[0]), .out(out_4[0]), .sel(in_3));
  Multiplexer #(.enable("false")) multiplexer_2 (.in0(in_1[1]), .in1(in_2[1]), .out(out_4[1]), .sel(in_3));
  Multiplexer #(.enable("false")) multiplexer_3 (.in0(in_1[2]), .in1(in_2[2]), .out(out_4[2]), .sel(in_3));
  Multiplexer #(.enable("false")) multiplexer_4 (.in0(in_1[3]), .in1(in_2[3]), .out(out_4[3]), .sel(in_3));

  // Other names for the same wires on the sheet: INPUT1[3:0] = in_1; INPUT2[3:0] = in_2; OUTPUT[3:0] = out_4
endmodule
