// Logisim project 实验3-1.circ as structural Verilog: 1 circuit, main circuit main
module main (
  input  LD,
  input  CLR,
  input  D0,
  input  D1,
  input  D2,
  input  D3,
  input  ENP,
  input  ENT,
  output R0,
  output R1,
  output R2,
  output R3,
  output RCO
);

  wire and_1_out, and_2_out, and_3_out, and_4_out, and_5_out, and_6_out, and_7_out, and_8_out, and_10_out,
       and_11_out, and_12_out, and_13_out, and_14_out, and_15_out, and_16_out, and_17_out, Clk_out,
       d_ff_1_qn, d_ff_2_qn, d_ff_3_qn, d_ff_4_qn, not_1_out, not_2_out, not_3_out, or_1_out, or_2_out,
       or_3_out, or_4_out, xor_1_out, xor_2_out, xor_3_out, xor_4_out;

  Clock Clk (.out(Clk_out));
  not not_1 (not_1_out, Clk_out);
  not not_2 (not_2_out, d_ff_1_qn);
  and and_1 (and_1_out, ~d_ff_1_qn, ~d_ff_2_qn);  // AND_Gate
  and and_2 (and_2_out, ~d_ff_3_qn, ~d_ff_2_qn, ~d_ff_1_qn);  // AND_Gate
  not not_3 (not_3_out, ENT);
  and and_3 (and_3_out, LD, ~CLR);  // AND_Gate
  and and_4 (and_4_out, ~and_3_out, ~CLR);  // AND_Gate
  and and_5 (and_5_out, not_2_out, and_8_out);
  and and_6 (and_6_out, and_1_out, and_8_out);
  and and_7 (and_7_out, and_2_out, and_8_out);
  and and_8 (and_8_out, ENP, ENT);
  xor xor_1 (xor_1_out, and_8_out, ~d_ff_1_qn);  // XOR_Gate
  xor xor_2 (xor_2_out, and_5_out, ~d_ff_2_qn);  // XOR_Gate
  xor xor_3 (xor_3_out, and_6_out, ~d_ff_3_qn);  // XOR_Gate
  xor xor_4 (xor_4_out, and_7_out, ~d_ff_4_qn);  // XOR_Gate
  and and_9 (RCO, ~d_ff_4_qn, ~d_ff_3_qn, ~d_ff_2_qn, ~d_ff_1_qn, ~not_3_out);  // AND_Gate
  and and_10 (and_10_out, D0, and_3_out);
  and and_11 (and_11_out, xor_1_out, and_4_out);
  and and_12 (and_12_out, D1, and_3_out);
  and and_13 (and_13_out, xor_2_out, and_4_out);
  and and_14 (and_14_out, D2, and_3_out);
  and and_15 (and_15_out, xor_3_out, and_4_out);
  and and_16 (and_16_out, D3, and_3_out);
  and and_17 (and_17_out, xor_4_out, and_4_out);
  or or_1 (or_1_out, and_10_out, and_11_out);
  or or_2 (or_2_out, and_12_out, and_13_out);
  or or_3 (or_3_out, and_14_out, and_15_out);
  or or_4 (or_4_out, and_16_out, and_17_out);
  D_Flip_Flop #(.trigger("falling")) d_ff_1 (
    .clk(not_1_out), .D(or_1_out), .Q(R0), .Qn(d_ff_1_qn));  // open: preset, reset
  D_Flip_Flop #(.trigger("falling")) d_ff_2 (
    .clk(not_1_out), .D(or_2_out), .Q(R1), .Qn(d_ff_2_qn));  // open: preset, reset
  D_Flip_Flop #(.trigger("falling")) d_ff_3 (
    .clk(not_1_out), .D(or_3_out), .Q(R2), .Qn(d_ff_3_qn));  // open: preset, reset
  D_Flip_Flop #(.trigger("falling")) d_ff_4 (
    .clk(not_1_out), .D(or_4_out), .Q(R3), .Qn(d_ff_4_qn));  // open: preset, reset

  // Notes on the sheet:
  //   两个与门上面的是控制清零和置位 下面的是用于计数（每次加一）
endmodule
