// Logisim project 实验3-2.circ as structural Verilog: 2 circuits, main circuit main
module main (
  input  in_1,
  input  [3:0] in_2,
  input  [3:0] in_3,
  input  [3:0] in_4,
  input  [3:0] in_5,
  input  [3:0] in_6,
  input  [3:0] in_7,
  input  ENP,
  input  ENT
);

  wire and_1_out, and_2_out, and_5_out, and_6_out, and_7_out, CLK, EN, LED, or_1_out;
  wire [3:0] H1, H2, M1, M2, S1, S2;

  Clock clock_1 (.out(CLK));
  or or_1 (or_1_out, and_1_out, and_2_out);
  Hex_Digit_Display hex_digit_display_1 (.value(H1), .dp(1'b1));
  Hex_Digit_Display hex_digit_display_2 (.value(H2));  // open: dp
  \四位计数器  \u_四位计数器_1  (
    .LD(in_1), .CLR(EN), .D0(in_2[0]), .D1(in_2[1]), .D2(in_2[2]), .D3(in_2[3]), .ENP(ENP), .ENT(or_1_out),
    .R0(H2[0]), .R1(H2[1]), .R2(H2[2]), .R3(H2[3]), .CLK(CLK));  // open: RCO
  \四位计数器  \u_四位计数器_2  (
    .LD(in_1), .CLR(or_1_out), .D0(in_3[0]), .D1(in_3[1]), .D2(in_3[2]), .D3(in_3[3]), .ENP(ENP), .ENT(LED),
    .R0(H1[0]), .R1(H1[1]), .R2(H1[2]), .R3(H1[3]), .CLK(CLK));  // open: RCO
  and and_1 (and_1_out, H2[1], H1[0], H1[1], LED);
  and and_2 (and_2_out, H1[0], H1[3], LED);
  Hex_Digit_Display hex_digit_display_3 (.value(M2));  // open: dp
  and and_3 (EN, or_1_out, H2[1]);
  Hex_Digit_Display hex_digit_display_4 (.value(M1), .dp(1'b1));
  Hex_Digit_Display hex_digit_display_5 (.value(S2));  // open: dp
  Hex_Digit_Display hex_digit_display_6 (.value(S1), .dp(1'b1));
  \四位计数器  \u_四位计数器_3  (
    .LD(in_1), .CLR(LED), .D0(in_4[0]), .D1(in_4[1]), .D2(in_4[2]), .D3(in_4[3]), .ENP(ENP), .ENT(and_5_out),
    .R0(M2[0]), .R1(M2[1]), .R2(M2[2]), .R3(M2[3]), .CLK(CLK));  // open: RCO
  \四位计数器  \u_四位计数器_4  (
    .LD(in_1), .CLR(and_5_out), .D0(in_5[0]), .D1(in_5[1]), .D2(in_5[2]), .D3(in_5[3]), .ENP(ENP),
    .ENT(and_7_out), .R0(M1[0]), .R1(M1[1]), .R2(M1[2]), .R3(M1[3]), .CLK(CLK));  // open: RCO
  and and_4 (LED, M2[2], M2[0], and_5_out);
  and and_5 (and_5_out, M1[3], M1[0], and_7_out);
  LED led_1 (.in(LED));
  // Buzzer buzzer_1: pin names not known; wires that end beside it: EN
  \四位计数器  \u_四位计数器_5  (
    .LD(in_1), .CLR(and_7_out), .D0(in_6[0]), .D1(in_6[1]), .D2(in_6[2]), .D3(in_6[3]), .ENP(ENP),
    .ENT(and_6_out), .R0(S2[0]), .R1(S2[1]), .R2(S2[2]), .R3(S2[3]), .CLK(CLK));  // open: RCO
  \四位计数器  \u_四位计数器_6  (
    .LD(in_1), .CLR(and_6_out), .D0(in_7[0]), .D1(in_7[1]), .D2(in_7[2]), .D3(in_7[3]), .ENP(ENP), .ENT(ENT),
    .R0(S1[0]), .R1(S1[1]), .R2(S1[2]), .R3(S1[3]), .CLK(CLK));  // open: RCO
  and and_6 (and_6_out, S1[3], S1[0]);
  and and_7 (and_7_out, S2[2], S2[0], and_6_out);

  // Other names for the same wires on the sheet: Hour_1[3:0] = in_2; Hour_2[3:0] = in_3; LD = in_1; Min_1[3:0] = in_4;
  //   Min_2[3:0] = in_5; Sec_1[3:0] = in_6; Sec_2[3:0] = in_7
endmodule

module \四位计数器  (
  input  CLK,
  input  LD,
  input  CLR,
  input  D0,
  input  D1,
  input  D2,
  input  D3,
  input  ENP,
  input  ENT,
  output R0,
  output R1,
  output R2,
  output R3,
  output RCO
);

  wire and_1_out, and_2_out, and_3_out, and_4_out, and_5_out, and_6_out, and_7_out, and_8_out, and_10_out,
       and_11_out, and_12_out, and_13_out, and_14_out, and_15_out, and_16_out, and_17_out, d_ff_1_qn,
       d_ff_2_qn, d_ff_3_qn, d_ff_4_qn, not_1_out, not_2_out, not_3_out, or_1_out, or_2_out, or_3_out,
       or_4_out, xor_1_out, xor_2_out, xor_3_out, xor_4_out;

  not not_1 (not_1_out, CLK);
  not not_2 (not_2_out, d_ff_1_qn);
  and and_1 (and_1_out, ~d_ff_1_qn, ~d_ff_2_qn);  // AND_Gate
  and and_2 (and_2_out, ~d_ff_3_qn, ~d_ff_2_qn, ~d_ff_1_qn);  // AND_Gate
  not not_3 (not_3_out, ENT);
  and and_3 (and_3_out, LD, ~CLR);  // AND_Gate
  and and_4 (and_4_out, ~and_3_out, ~CLR);  // AND_Gate
  and and_5 (and_5_out, not_2_out, and_8_out);
  and and_6 (and_6_out, and_1_out, and_8_out);
  and and_7 (and_7_out, and_2_out, and_8_out);
  and and_8 (and_8_out, ENP, ENT);
  xor xor_1 (xor_1_out, and_8_out, ~d_ff_1_qn);  // XOR_Gate
  xor xor_2 (xor_2_out, and_5_out, ~d_ff_2_qn);  // XOR_Gate
  xor xor_3 (xor_3_out, and_6_out, ~d_ff_3_qn);  // XOR_Gate
  xor xor_4 (xor_4_out, and_7_out, ~d_ff_4_qn);  // XOR_Gate
  and and_9 (RCO, ~d_ff_4_qn, ~d_ff_3_qn, ~d_ff_2_qn, ~d_ff_1_qn, ~not_3_out);  // AND_Gate
  and and_10 (and_10_out, D0, and_3_out);
  and and_11 (and_11_out, xor_1_out, and_4_out);
  and and_12 (and_12_out, D1, and_3_out);
  and and_13 (and_13_out, xor_2_out, and_4_out);
  and and_14 (and_14_out, D2, and_3_out);
  and and_15 (and_15_out, xor_3_out, and_4_out);
  and and_16 (and_16_out, D3, and_3_out);
  and and_17 (and_17_out, xor_4_out, and_4_out);
  or or_1 (or_1_out, and_10_out, and_11_out);
  or or_2 (or_2_out, and_12_out, and_13_out);
  or or_3 (or_3_out, and_14_out, and_15_out);
  or or_4 (or_4_out, and_16_out, and_17_out);
  D_Flip_Flop #(.trigger("falling")) d_ff_1 (
    .clk(not_1_out), .D(or_1_out), .Q(R0), .Qn(d_ff_1_qn));  // open: preset, reset
  D_Flip_Flop #(.trigger("falling")) d_ff_2 (
    .clk(not_1_out), .D(or_2_out), .Q(R1), .Qn(d_ff_2_qn));  // open: preset, reset
  D_Flip_Flop #(.trigger("falling")) d_ff_3 (
    .clk(not_1_out), .D(or_3_out), .Q(R2), .Qn(d_ff_3_qn));  // open: preset, reset
  D_Flip_Flop #(.trigger("falling")) d_ff_4 (
    .clk(not_1_out), .D(or_4_out), .Q(R3), .Qn(d_ff_4_qn));  // open: preset, reset

  // Notes on the sheet:
  //   两个与门上面的是控制清零和置位 下面的是用于计数（每次加一）
endmodule
