// Logisim project 实验3-3.circ as structural Verilog: 1 circuit, main circuit main
module main (
  input  CLR,
  input  D3,
  input  D2,
  input  D1,
  input  D0,
  input  LIN,
  input  S0,
  input  S1,
  output Q3,
  output Q2,
  output Q1,
  output Q0
);

  wire CLK_out, multiplexer_1_out, multiplexer_2_out, multiplexer_3_out, multiplexer_4_out, not_1_out,
       not_2_out, xor_1_out;

  Clock CLK (.out(CLK_out));
  not not_1 (not_1_out, CLK_out);
  not not_2 (not_2_out, CLR);
  Multiplexer #(.select(2), .enable("false")) multiplexer_1 (
    .in0(Q3), .in1(Q2), .in2(xor_1_out), .in3(D3), .out(multiplexer_1_out), .sel({S1, S0}));
  Multiplexer #(.select(2), .enable("false")) multiplexer_2 (
    .in0(Q2), .in1(Q1), .in2(Q3), .in3(D2), .out(multiplexer_2_out), .sel({S1, S0}));
  Multiplexer #(.select(2), .enable("false")) multiplexer_3 (
    .in0(Q1), .in1(Q0), .in2(Q2), .in3(D1), .out(multiplexer_3_out), .sel({S1, S0}));
  Multiplexer #(.select(2), .enable("false")) multiplexer_4 (
    .in0(Q0), .in1(LIN), .in2(Q1), .in3(D0), .out(multiplexer_4_out), .sel({S1, S0}));
  D_Flip_Flop #(.trigger("falling")) d_ff_1 (
    .clk(not_1_out), .D(multiplexer_1_out), .Q(Q3), .reset(not_2_out));  // open: Qn, preset
  D_Flip_Flop #(.trigger("falling")) d_ff_2 (
    .clk(not_1_out), .D(multiplexer_2_out), .Q(Q2), .reset(not_2_out));  // open: Qn, preset
  D_Flip_Flop #(.trigger("falling")) d_ff_3 (
    .clk(not_1_out), .D(multiplexer_3_out), .Q(Q1), .reset(not_2_out));  // open: Qn, preset
  D_Flip_Flop #(.trigger("falling")) d_ff_4 (
    .clk(not_1_out), .D(multiplexer_4_out), .Q(Q0), .reset(not_2_out));  // open: Qn, preset
  xor xor_1 (xor_1_out, Q1, Q0);
endmodule
