// Logisim project 实验3-4.circ as structural Verilog: 2 circuits, main circuit main
module main (
  input  [3:0] in_1,
  input  [3:0] in_2,
  input  [2:0] in_3,
  input  [2:0] in_4,
  input  [3:0] in_5,
  output [7:0] out_6,
  output out_7
);

  wire adder_1_cout, clock_1_out, Load, not_1_out, Rst, \八位右移器_1_out_6 ;
  wire [2:0] counter_1_q;
  wire [3:0] adder_1_out, multiplexer_1_out, multiplexer_2_out, \八位右移器_1_out_4 , \八位右移器_1_out_5 ;

  Hex_Digit_Display hex_digit_display_1 (.value(in_1));  // open: dp
  Button button_1 (.out(Rst));
  Clock clock_1 (.out(clock_1_out));
  Multiplexer #(.width(4), .enable("false")) multiplexer_1 (
    .in0(in_5), .in1(in_1), .out(multiplexer_1_out), .sel(\八位右移器_1_out_6 ));
  not not_1 (not_1_out, out_7);
  Adder #(.width(4)) adder_1 (
    .a(out_6[7:4]), .b(multiplexer_1_out), .out(adder_1_out), .cout(adder_1_cout));  // open: cin
  Hex_Digit_Display hex_digit_display_2 (.value(in_2));  // open: dp
  \八位右移器  \u_八位右移器_1  (
    .\高位 (adder_1_out), .\低位 (out_6[3:0]), .Rin(adder_1_cout), .out_4(\八位右移器_1_out_4 ),
    .out_5(\八位右移器_1_out_5 ), .out_6(\八位右移器_1_out_6 ));
  Register #(.width(4), .Select("low")) register_1 (
    .D(\八位右移器_1_out_4 ), .en(not_1_out), .Q(out_6[7:4]), .clk(clock_1_out), .clr(Rst));
  Hex_Digit_Display hex_digit_display_3 (.value(out_6[3:0]));  // open: dp
  Hex_Digit_Display hex_digit_display_4 (.value(out_6[7:4]));  // open: dp
  Register #(.width(4), .Select("low")) register_2 (
    .D(multiplexer_2_out), .en(not_1_out), .Q(out_6[3:0]), .clk(clock_1_out), .clr(Rst));
  Multiplexer #(.width(4), .enable("false")) multiplexer_2 (
    .in0(\八位右移器_1_out_5 ), .in1(in_2), .out(multiplexer_2_out), .sel(Load));
  Counter #(.width(3), .max('h7), .ongoal("stay")) counter_1 (
    .Q(counter_1_q), .clk(clock_1_out), .clr(Rst));  // open: load, D, count, carry, preset, down
  Comparator #(.width(3), .mode("unsigned")) comparator_1 (.a(counter_1_q), .b(in_3), .eq(Load));  // open: gt, lt
  Comparator #(.width(3), .mode("unsigned")) comparator_2 (.a(counter_1_q), .b(in_4), .gt(out_7));  // open: eq, lt

  // Other names for the same wires on the sheet: Stop = out_7; X[3:0] = in_1; Y[3:0] = in_2; Z[7:0] = out_6
endmodule

module \八位右移器  (
  input  [3:0] \高位 ,
  input  [3:0] \低位 ,
  input  Rin,
  output [3:0] out_4,
  output [3:0] out_5,
  output out_6
);


  assign out_4 = {Rin, \高位 [3:1]};
  assign out_5 = {\高位 [0], \低位 [3:1]};
  assign out_6 = \低位 [0];

  // Other names for the same wires on the sheet: 低位输出[3:0] = {\高位 [0], \低位 [3:1]}; 高位输出[3:0] = {Rin, \高位 [3:1]}
endmodule
