// Logisim project 实验3-5.circ as structural Verilog: 2 circuits, main circuit main
module main (
  input  [4:0] R1_num,
  input  [4:0] R2_num,
  input  [31:0] Din,
  input  [4:0] Write_Reg_num,
  input  Write_Enable,
  input  CLK,
  output [31:0] Reg1Out,
  output [31:0] Reg2Out
);

  regfiles regfiles_1 (
    .R1_num(R1_num), .R2_num(R2_num), .in_3(Din), .Write_Reg_num(Write_Reg_num), .Write_Enable(Write_Enable),
    .Clock(CLK), .Reg1Out(Reg1Out), .Reg2Out(Reg2Out));
endmodule

module regfiles (
  input  [4:0] R1_num,
  input  [4:0] R2_num,
  input  [31:0] in_3,
  input  [4:0] Write_Reg_num,
  input  Write_Enable,
  input  Clock,
  output [31:0] Reg1Out,
  output [31:0] Reg2Out
);

  wire and_1_out, and_2_out, and_3_out, and_4_out, and_5_out, and_6_out, and_7_out, and_8_out, and_9_out,
       and_10_out, and_11_out, and_12_out, and_13_out, and_14_out, and_15_out, and_16_out, and_17_out,
       and_18_out, and_19_out, and_20_out, and_21_out, and_22_out, and_23_out, and_24_out, and_25_out,
       and_26_out, and_27_out, and_28_out, and_29_out, and_30_out, and_31_out, and_32_out, decoder_1_out0,
       decoder_1_out1, decoder_1_out2, decoder_1_out3, decoder_1_out4, decoder_1_out5, decoder_1_out6,
       decoder_1_out7, decoder_1_out8, decoder_1_out9, decoder_1_out10, decoder_1_out11, decoder_1_out12,
       decoder_1_out13, decoder_1_out14, decoder_1_out15;
  wire [15:0] decoder_1_out16;
  wire [31:0] _1, _2, _3, _4, _5, _6, _7, _8, _9, _10, _11, _12, _13, _14, _15, _16, _17, _18, _19, _20, _21,
       _22, _23, _24, _25, _26, _27, _28, _29, _30, _31, _32;

  Decoder #(.select(5), .enable("false")) decoder_1 (
    .out0(decoder_1_out0), .out1(decoder_1_out1), .out2(decoder_1_out2), .out3(decoder_1_out3),
    .out4(decoder_1_out4), .out5(decoder_1_out5), .out6(decoder_1_out6), .out7(decoder_1_out7),
    .out8(decoder_1_out8), .out9(decoder_1_out9), .out10(decoder_1_out10), .out11(decoder_1_out11),
    .out12(decoder_1_out12), .out13(decoder_1_out13), .out14(decoder_1_out14), .out15(decoder_1_out15),
    .out16(decoder_1_out16[0]), .out17(decoder_1_out16[1]), .out18(decoder_1_out16[2]),
    .out19(decoder_1_out16[3]), .out20(decoder_1_out16[4]), .out21(decoder_1_out16[5]),
    .out22(decoder_1_out16[6]), .out23(decoder_1_out16[7]), .out24(decoder_1_out16[8]),
    .out25(decoder_1_out16[9]), .out26(decoder_1_out16[10]), .out27(decoder_1_out16[11]),
    .out28(decoder_1_out16[12]), .out29(decoder_1_out16[13]), .out30(decoder_1_out16[14]),
    .out31(decoder_1_out16[15]), .sel(Write_Reg_num));
  and and_1 (and_1_out, Write_Enable, decoder_1_out0);
  and and_2 (and_2_out, Write_Enable, decoder_1_out1);
  and and_3 (and_3_out, Write_Enable, decoder_1_out2);
  and and_4 (and_4_out, Write_Enable, decoder_1_out3);
  and and_5 (and_5_out, Write_Enable, decoder_1_out4);
  and and_6 (and_6_out, Write_Enable, decoder_1_out5);
  and and_7 (and_7_out, Write_Enable, decoder_1_out6);
  and and_8 (and_8_out, Write_Enable, decoder_1_out7);
  and and_9 (and_9_out, Write_Enable, decoder_1_out8);
  and and_10 (and_10_out, Write_Enable, decoder_1_out9);
  and and_11 (and_11_out, Write_Enable, decoder_1_out10);
  and and_12 (and_12_out, Write_Enable, decoder_1_out11);
  and and_13 (and_13_out, Write_Enable, decoder_1_out12);
  and and_14 (and_14_out, Write_Enable, decoder_1_out13);
  and and_15 (and_15_out, Write_Enable, decoder_1_out14);
  and and_16 (and_16_out, Write_Enable, decoder_1_out15);
  Register #(.width(32), .Select("low")) register_1 (.D({32{1'b0}}), .en(and_1_out), .Q(_1), .clk(Clock));  // open: clr
  Register #(.width(32), .Select("low")) register_2 (.D(in_3), .en(and_2_out), .Q(_2), .clk(Clock));  // open: clr
  Register #(.width(32), .Select("low")) register_3 (.D(in_3), .en(and_3_out), .Q(_3), .clk(Clock));  // open: clr
  Register #(.width(32), .Select("low")) register_4 (.D(in_3), .en(and_4_out), .Q(_4), .clk(Clock));  // open: clr
  Register #(.width(32), .Select("low")) register_5 (.D(in_3), .en(and_5_out), .Q(_5), .clk(Clock));  // open: clr
  Register #(.width(32), .Select("low")) register_6 (.D(in_3), .en(and_6_out), .Q(_6), .clk(Clock));  // open: clr
  Register #(.width(32), .Select("low")) register_7 (.D(in_3), .en(and_7_out), .Q(_7), .clk(Clock));  // open: clr
  Register #(.width(32), .Select("low")) register_8 (.D(in_3), .en(and_8_out), .Q(_8), .clk(Clock));  // open: clr
  Register #(.width(32), .Select("low")) register_9 (.D(in_3), .en(and_9_out), .Q(_9), .clk(Clock));  // open: clr
  Register #(.width(32), .Select("low")) register_10 (.D(in_3), .en(and_10_out), .Q(_10), .clk(Clock));  // open: clr
  Register #(.width(32), .Select("low")) register_11 (.D(in_3), .en(and_11_out), .Q(_11), .clk(Clock));  // open: clr
  Register #(.width(32), .Select("low")) register_12 (.D(in_3), .en(and_12_out), .Q(_12), .clk(Clock));  // open: clr
  Register #(.width(32), .Select("low")) register_13 (.D(in_3), .en(and_13_out), .Q(_13), .clk(Clock));  // open: clr
  Register #(.width(32), .Select("low")) register_14 (.D(in_3), .en(and_14_out), .Q(_14), .clk(Clock));  // open: clr
  Register #(.width(32), .Select("low")) register_15 (.D(in_3), .en(and_15_out), .Q(_15), .clk(Clock));  // open: clr
  Register #(.width(32), .Select("low")) register_16 (.D(in_3), .en(and_16_out), .Q(_16), .clk(Clock));  // open: clr
  and and_17 (and_17_out, Write_Enable, decoder_1_out16[0]);
  and and_18 (and_18_out, Write_Enable, decoder_1_out16[1]);
  and and_19 (and_19_out, Write_Enable, decoder_1_out16[2]);
  and and_20 (and_20_out, Write_Enable, decoder_1_out16[3]);
  and and_21 (and_21_out, Write_Enable, decoder_1_out16[4]);
  and and_22 (and_22_out, Write_Enable, decoder_1_out16[5]);
  and and_23 (and_23_out, Write_Enable, decoder_1_out16[6]);
  and and_24 (and_24_out, Write_Enable, decoder_1_out16[7]);
  and and_25 (and_25_out, Write_Enable, decoder_1_out16[8]);
  and and_26 (and_26_out, Write_Enable, decoder_1_out16[9]);
  and and_27 (and_27_out, Write_Enable, decoder_1_out16[10]);
  and and_28 (and_28_out, Write_Enable, decoder_1_out16[11]);
  and and_29 (and_29_out, Write_Enable, decoder_1_out16[12]);
  and and_30 (and_30_out, Write_Enable, decoder_1_out16[13]);
  and and_31 (and_31_out, Write_Enable, decoder_1_out16[14]);
  and and_32 (and_32_out, Write_Enable, decoder_1_out16[15]);
  Register #(.width(32), .Select("low")) register_17 (.D(in_3), .en(and_17_out), .Q(_17), .clk(Clock));  // open: clr
  Register #(.width(32), .Select("low")) register_18 (.D(in_3), .en(and_18_out), .Q(_18), .clk(Clock));  // open: clr
  Register #(.width(32), .Select("low")) register_19 (.D(in_3), .en(and_19_out), .Q(_19), .clk(Clock));  // open: clr
  Register #(.width(32), .Select("low")) register_20 (.D(in_3), .en(and_20_out), .Q(_20), .clk(Clock));  // open: clr
  Register #(.width(32), .Select("low")) register_21 (.D(in_3), .en(and_21_out), .Q(_21), .clk(Clock));  // open: clr
  Register #(.width(32), .Select("low")) register_22 (.D(in_3), .en(and_22_out), .Q(_22), .clk(Clock));  // open: clr
  Register #(.width(32), .Select("low")) register_23 (.D(in_3), .en(and_23_out), .Q(_23), .clk(Clock));  // open: clr
  Register #(.width(32), .Select("low")) register_24 (.D(in_3), .en(and_24_out), .Q(_24), .clk(Clock));  // open: clr
  Register #(.width(32), .Select("low")) register_25 (.D(in_3), .en(and_25_out), .Q(_25), .clk(Clock));  // open: clr
  Register #(.width(32), .Select("low")) register_26 (.D(in_3), .en(and_26_out), .Q(_26), .clk(Clock));  // open: clr
  Register #(.width(32), .Select("low")) register_27 (.D(in_3), .en(and_27_out), .Q(_27), .clk(Clock));  // open: clr
  Register #(.width(32), .Select("low")) register_28 (.D(in_3), .en(and_28_out), .Q(_28), .clk(Clock));  // open: clr
  Register #(.width(32), .Select("low")) register_29 (.D(in_3), .en(and_29_out), .Q(_29), .clk(Clock));  // open: clr
  Register #(.width(32), .Select("low")) register_30 (.D(in_3), .en(and_30_out), .Q(_30), .clk(Clock));  // open: clr
  Register #(.width(32), .Select("low")) register_31 (.D(in_3), .en(and_31_out), .Q(_31), .clk(Clock));  // open: clr
  Register #(.width(32), .Select("low")) register_32 (.D(in_3), .en(and_32_out), .Q(_32), .clk(Clock));  // open: clr
  Multiplexer #(.select(5), .width(32), .enable("false")) multiplexer_1 (
    .in0(_1), .in1(_2), .in2(_3), .in3(_4), .in4(_5), .in5(_6), .in6(_7), .in7(_8), .in8(_9), .in9(_10),
    .in10(_11), .in11(_12), .in12(_13), .in13(_14), .in14(_15), .in15(_16), .in16(_17), .in17(_18),
    .in18(_19), .in19(_20), .in20(_21), .in21(_22), .in22(_23), .in23(_24), .in24(_25), .in25(_26),
    .in26(_27), .in27(_28), .in28(_29), .in29(_30), .in30(_31), .in31(_32), .out(Reg1Out), .sel(R1_num));
  Multiplexer #(.select(5), .width(32), .enable("false")) multiplexer_2 (
    .in0(_1), .in1(_2), .in2(_3), .in3(_4), .in4(_5), .in5(_6), .in6(_7), .in7(_8), .in8(_9), .in9(_10),
    .in10(_11), .in11(_12), .in12(_13), .in13(_14), .in14(_15), .in15(_16), .in16(_17), .in17(_18),
    .in18(_19), .in19(_20), .in20(_21), .in21(_22), .in22(_23), .in23(_24), .in24(_25), .in25(_26),
    .in26(_27), .in27(_28), .in28(_29), .in29(_30), .in30(_31), .in31(_32), .out(Reg2Out), .sel(R2_num));

  // Other names for the same wires on the sheet: CLK = Clock; Din[31:0] = in_3; RA[4:0] = R1_num; RB[4:0] = R2_num;
  //   RDA[31:0] = Reg1Out; RDB[31:0] = Reg2Out; RW[4:0] = Write_Reg_num; WE = Write_Enable
endmodule
