// Logisim project 实验2-3.circ as structural Verilog: 3 circuits, main circuit main
module Adder (
  input  A,
  input  B,
  input  Cin,
  output F,
  output Cout
);

  wire and_1_out, and_2_out, and_3_out;

  and and_1 (and_1_out, A, B);
  and and_2 (and_2_out, A, Cin);
  and and_3 (and_3_out, B, Cin);
  xor xor_1 (F, A, B, Cin);
  or or_1 (Cout, and_1_out, and_2_out, and_3_out);
endmodule

module main (
  input  [3:0] X,
  input  [3:0] Y,
  input  Cin,
  output [3:0] out_4,
  output out_5,
  output out_6,
  output Cout,
  output out_8,
  output out_9
);

  wire adder_1_cout, adder_1_f, adder_2_cout, adder_2_f, adder_3_cout, adder_3_f, adder_4_cout, sub_1_bout,
       sub_1_f, sub_2_bout, sub_2_f, sub_3_bout, sub_3_f, sub_4_bout, sub_4_f;

  Hex_Digit_Display hex_digit_display_1 (.value(X));  // open: dp
  Adder adder_1 (.A(X[0]), .B(Y[0]), .Cin(1'b0), .F(adder_1_f), .Cout(adder_1_cout));
  Sub sub_1 (.A(X[0]), .B(Y[0]), .Bin(1'b0), .F(sub_1_f), .Bout(sub_1_bout));
  Adder adder_2 (.A(X[1]), .B(Y[1]), .Cin(adder_1_cout), .F(adder_2_f), .Cout(adder_2_cout));
  Sub sub_2 (.A(X[1]), .B(Y[1]), .Bin(sub_1_bout), .F(sub_2_f), .Bout(sub_2_bout));
  Hex_Digit_Display hex_digit_display_2 (.value(Y));  // open: dp
  Adder adder_3 (.A(X[2]), .B(Y[2]), .Cin(adder_2_cout), .F(adder_3_f), .Cout(adder_3_cout));
  Sub sub_3 (.A(X[2]), .B(Y[2]), .Bin(sub_2_bout), .F(sub_3_f), .Bout(sub_3_bout));
  Adder adder_4 (.A(X[3]), .B(Y[3]), .Cin(adder_3_cout), .F(out_8), .Cout(adder_4_cout));
  Sub sub_4 (.A(X[3]), .B(Y[3]), .Bin(sub_3_bout), .F(sub_4_f), .Bout(sub_4_bout));
  xor xor_1 (out_5, adder_4_cout, adder_3_cout);
  Multiplexer #(.enable("false")) multiplexer_1 (.in0(adder_1_f), .in1(sub_1_f), .out(out_4[0]), .sel(Cin));
  Multiplexer #(.enable("false")) multiplexer_2 (.in0(adder_2_f), .in1(sub_2_f), .out(out_4[1]), .sel(Cin));
  nor nor_1 (out_6, adder_1_f, adder_2_f, adder_3_f, out_8);
  Multiplexer #(.enable("false")) multiplexer_3 (.in0(adder_3_f), .in1(sub_3_f), .out(out_4[2]), .sel(Cin));
  Multiplexer #(.enable("false")) multiplexer_4 (.in0(out_8), .in1(sub_4_f), .out(out_4[3]), .sel(Cin));
  Multiplexer #(.enable("false")) multiplexer_5 (.in0(adder_4_cout), .in1(sub_4_bout), .out(Cout), .sel(Cin));
  Hex_Digit_Display hex_digit_display_3 (.value(out_4));  // open: dp
  xor xor_2 (out_9, Cout, Cin);

  // Other names for the same wires on the sheet: ans[3:0] = out_4; CF = out_9; numX[3:0] = X; numY[3:0] = Y;
  //   OF = out_5; SF = out_8; ZF = out_6
endmodule

module Sub (
  input  A,
  input  B,
  input  Bin,
  output F,
  output Bout
);

  wire and_1_out, and_2_out, and_3_out, not_1_out, not_2_out, or_1_out;

  not not_1 (not_1_out, B);
  not not_2 (not_2_out, Bin);
  xor xor_1 (F, A, not_1_out, not_2_out);
  and and_1 (and_1_out, A, not_1_out);
  and and_2 (and_2_out, A, not_2_out);
  and and_3 (and_3_out, not_1_out, not_2_out);
  or or_1 (or_1_out, and_1_out, and_2_out, and_3_out);
  not not_3 (Bout, or_1_out);
endmodule
