// Logisim project 实验2-4.circ as structural Verilog: 2 circuits, main circuit main
module main (
  input  [6:0] in_1,
  input  EN,
  output OK,
  output Error,
  output [6:0] Output
);

  wire decoder_1_out1, decoder_1_out2, decoder_1_out3, decoder_1_out4, decoder_1_out5, decoder_1_out6,
       decoder_1_out7;
  wire [2:0] Wrong_digit;

  XOR xor_1 (.D0(in_1[0]), .D1(in_1[2]), .D2(in_1[4]), .D3(in_1[6]), .F(Wrong_digit[0]));
  XOR xor_2 (.D0(in_1[1]), .D1(in_1[2]), .D2(in_1[5]), .D3(in_1[6]), .F(Wrong_digit[1]));
  XOR xor_3 (.D0(in_1[3]), .D1(in_1[4]), .D2(in_1[5]), .D3(in_1[6]), .F(Wrong_digit[2]));
  Decoder #(.select(3)) decoder_1 (
    .out0(OK), .out1(decoder_1_out1), .out2(decoder_1_out2), .out3(decoder_1_out3), .out4(decoder_1_out4),
    .out5(decoder_1_out5), .out6(decoder_1_out6), .out7(decoder_1_out7), .sel(Wrong_digit), .en(EN));
  not not_1 (Error, OK);
  xor xor_4 (Output[0], in_1[0], decoder_1_out1);
  xor xor_5 (Output[1], in_1[1], decoder_1_out2);
  xor xor_6 (Output[2], in_1[2], decoder_1_out3);
  xor xor_7 (Output[3], in_1[3], decoder_1_out4);
  xor xor_8 (Output[4], in_1[4], decoder_1_out5);
  xor xor_9 (Output[5], in_1[5], decoder_1_out6);
  xor xor_10 (Output[6], in_1[6], decoder_1_out7);
  Hex_Digit_Display hex_digit_display_1 (.value({1'b0, Wrong_digit}));  // open: dp

  // Other names for the same wires on the sheet: Input[6:0] = in_1
endmodule

module XOR (
  input  D0,
  input  D1,
  input  D2,
  input  D3,
  output F
);

  wire xor_1_out, xor_2_out;

  xor xor_1 (xor_1_out, D0, D1);
  xor xor_2 (xor_2_out, xor_1_out, D2);
  xor xor_3 (F, xor_2_out, D3);
endmodule
