// Logisim project 实验2-5.circ as structural Verilog: 4 circuits, main circuit main
module main (
  input  [7:0] DataIn,
  input  [2:0] shamt,
  input  L_R,
  input  A_L,
  output [7:0] Output
);

  wire [0:0] not_1_out;
  wire [7:0] multiplexer_1_out, multiplexer_2_out, shift1_1_out_l, shift1_1_out_r, shift2_1_out_l,
       shift2_1_out_r, shift_1_out_l, shift_1_out_r;

  shift shift_1 (.in_1(DataIn), .cin(A_L), .out_R(shift_1_out_r), .out_L(shift_1_out_l));
  not not_1 (not_1_out[0], L_R);
  Multiplexer #(.select(2), .width(8), .enable("false")) multiplexer_1 (
    .in0(DataIn), .in1(DataIn), .in2(shift_1_out_l), .in3(shift_1_out_r), .out(multiplexer_1_out),
    .sel({shamt[0], not_1_out[0]}));
  shift1 shift1_1 (.in_1(multiplexer_1_out), .A_L(A_L), .out_R(shift1_1_out_r), .out_L(shift1_1_out_l));
  Multiplexer #(.select(2), .width(8), .enable("false")) multiplexer_2 (
    .in0(multiplexer_1_out), .in1(multiplexer_1_out), .in2(shift1_1_out_l), .in3(shift1_1_out_r),
    .out(multiplexer_2_out), .sel({shamt[1], not_1_out[0]}));
  shift2 shift2_1 (.in_1(multiplexer_2_out), .A_L(A_L), .out_R(shift2_1_out_r), .out_L(shift2_1_out_l));
  Multiplexer #(.select(2), .width(8), .enable("false")) multiplexer_3 (
    .in0(multiplexer_2_out), .in1(multiplexer_2_out), .in2(shift2_1_out_l), .in3(shift2_1_out_r),
    .out(Output), .sel({shamt[2], not_1_out[0]}));

  // Other names for the same wires on the sheet: Arth_Logic = A_L; Data[7:0] = DataIn; Left_Right = L_R
endmodule

module shift (
  input  [7:0] in_1,
  input  cin,
  output [7:0] out_R,
  output [7:0] out_L
);

  Multiplexer #(.enable("false")) multiplexer_1 (.in0(1'b0), .in1(in_1[7]), .out(out_L[0]), .sel(cin));
  Multiplexer #(.enable("false")) multiplexer_2 (.in0(1'b0), .in1(in_1[0]), .out(out_R[7]), .sel(cin));

  assign out_L[7:1] = in_1[6:0];
  assign out_R[6:0] = in_1[7:1];

  // Other names for the same wires on the sheet: input[7:0] = in_1
endmodule

module shift1 (
  input  [7:0] in_1,
  input  A_L,
  output [7:0] out_R,
  output [7:0] out_L
);

  Multiplexer #(.enable("false")) multiplexer_1 (.in0(1'b0), .in1(in_1[7]), .out(out_L[1]), .sel(A_L));
  Multiplexer #(.enable("false")) multiplexer_2 (.in0(1'b0), .in1(in_1[0]), .out(out_R[6]), .sel(A_L));
  Multiplexer #(.enable("false")) multiplexer_3 (.in0(1'b0), .in1(in_1[6]), .out(out_L[0]), .sel(A_L));
  Multiplexer #(.enable("false")) multiplexer_4 (.in0(1'b0), .in1(in_1[1]), .out(out_R[7]), .sel(A_L));

  assign out_L[7:2] = in_1[5:0];
  assign out_R[5:0] = in_1[7:2];

  // Other names for the same wires on the sheet: input[7:0] = in_1
endmodule

module shift2 (
  input  [7:0] in_1,
  input  A_L,
  output [7:0] out_R,
  output [7:0] out_L
);

  Multiplexer #(.enable("false")) multiplexer_1 (.in0(1'b0), .in1(in_1[0]), .out(out_R[4]), .sel(A_L));
  Multiplexer #(.enable("false")) multiplexer_2 (.in0(1'b0), .in1(in_1[5]), .out(out_L[1]), .sel(A_L));
  Multiplexer #(.enable("false")) multiplexer_3 (.in0(1'b0), .in1(in_1[4]), .out(out_L[0]), .sel(A_L));
  Multiplexer #(.enable("false")) multiplexer_4 (.in0(1'b0), .in1(in_1[1]), .out(out_R[5]), .sel(A_L));
  Multiplexer #(.enable("false")) multiplexer_5 (.in0(1'b0), .in1(in_1[6]), .out(out_L[2]), .sel(A_L));
  Multiplexer #(.enable("false")) multiplexer_6 (.in0(1'b0), .in1(in_1[2]), .out(out_R[6]), .sel(A_L));
  Multiplexer #(.enable("false")) multiplexer_7 (.in0(1'b0), .in1(in_1[3]), .out(out_R[7]), .sel(A_L));
  Multiplexer #(.enable("false")) multiplexer_8 (.in0(1'b0), .in1(in_1[7]), .out(out_L[3]), .sel(A_L));

  assign out_L[7:4] = in_1[3:0];
  assign out_R[3:0] = in_1[7:4];

  // Other names for the same wires on the sheet: input[7:0] = in_1
endmodule
