// Logisim project 思考题4.circ as structural Verilog: 1 circuit, main circuit main
module main (
  input  [15:0] in_1,
  input  [15:0] in_2,
  input  [15:0] in_3,
  input  [15:0] in_4,
  input  [15:0] in_5,
  input  [15:0] in_6,
  input  [15:0] in_7,
  input  [15:0] in_8,
  input  [15:0] in_9,
  input  [15:0] in_10,
  input  [15:0] in_11,
  input  [15:0] in_12,
  input  [15:0] in_13,
  input  [15:0] in_14,
  input  [15:0] in_15,
  input  [15:0] in_16
);

  DotMatrix #(.matrixcols(16), .matrixrows(16)) dotmatrix_1 (
    .col0(in_1), .col1(in_3), .col2(in_5), .col3(in_7), .col4(in_9), .col5(in_11), .col6(in_13),
    .col7(in_15), .col8(in_16), .col9(in_14), .col10(in_12), .col11(in_10), .col12(in_8), .col13(in_6),
    .col14(in_4), .col15(in_2));
endmodule
