// Logisim project lab4.circ as structural Verilog: 26 circuits, main circuit main
module main (
);
endmodule

// CLU
module \_4位先行进位部件CLU  (
  input  P0,
  input  P1,
  input  P2,
  input  P3,
  input  G0,
  input  G1,
  input  G2,
  input  G3,
  input  C0,
  output C1,
  output C3,
  output C2,
  output C4,
  output Pg,
  output Gg
);

  wire and_1_out, and_2_out, and_3_out, and_4_out, and_5_out, and_6_out, and_7_out, and_8_out, and_9_out,
       and_10_out, and_11_out, and_12_out, and_13_out;

  and and_1 (and_1_out, C0, P0);
  and and_2 (and_2_out, G0, P1);
  and and_3 (and_3_out, C0, P0, P1);
  and and_4 (and_4_out, G1, P2);
  and and_5 (and_5_out, P2, P1, G0);
  and and_6 (and_6_out, P2, P1, P0, C0);
  and and_7 (and_7_out, G2, P3);
  and and_8 (and_8_out, G1, P3, P2);
  and and_9 (and_9_out, G0, P2, P3, P1);
  and and_10 (and_10_out, P0, P1, P2, P3, C0);
  or or_1 (C1, and_1_out, G0);
  or or_2 (C2, and_2_out, and_3_out, G1);
  or or_3 (C3, and_4_out, and_5_out, and_6_out, G2);
  or or_4 (C4, and_7_out, and_8_out, and_9_out, and_10_out, G3);
  and and_11 (and_11_out, G2, P3);
  and and_12 (and_12_out, G1, P2, P3);
  and and_13 (and_13_out, G0, P1, P2, P3);
  and and_14 (Pg, P0, P1, P2, P3);
  or or_5 (Gg, and_11_out, and_12_out, and_13_out, G3);

  // Notes on the sheet:
  //   输入引脚
  //   四位先行进位逻辑单元CLU，C0为进位输入， C1C2C3C4为进位输出，Pg、Gg为成组进位生成传递函数
  //   输出引脚
endmodule

module FA (
  input  A,
  input  B,
  input  Cin,
  output F,
  output P,
  output G
);

  and and_1 (G, A, B);
  or or_1 (P, B, A);
  xor xor_1 (F, A, B, Cin);

  // Notes on the sheet:
  //   全加器
endmodule

module \_4位快速加法器CLA  (
  input  [3:0] X,
  input  [3:0] Y,
  input  Cin,
  output [3:0] F,
  output Cout,
  output Pg,
  output Gg
);

  wire fa_1_g, fa_1_p, \n4位先行进位部件clu_1_c1 , \n4位先行进位部件clu_1_c2 , \n4位先行进位部件clu_1_c3 , \全加器_2_g , \全加器_2_p ,
       \全加器_3_g , \全加器_3_p , \全加器_g , \全加器_p ;

  FA \u_全加器  (.A(X[0]), .F(F[0]), .B(Y[0]), .P(\全加器_p ), .Cin(Cin), .G(\全加器_g ));
  Hex_Digit_Display hex_digit_display_1 (.value(X));  // open: dp
  FA \u_全加器_2  (.A(X[1]), .F(F[1]), .B(Y[1]), .P(\全加器_2_p ), .Cin(\n4位先行进位部件clu_1_c1 ), .G(\全加器_2_g ));
  Hex_Digit_Display hex_digit_display_2 (.value(Y));  // open: dp
  \_4位先行进位部件CLU  \u_4位先行进位部件clu_1  (
    .P0(\全加器_p ), .P1(\全加器_2_p ), .P2(fa_1_p), .P3(\全加器_3_p ), .C1(\n4位先行进位部件clu_1_c1 ),
    .C3(\n4位先行进位部件clu_1_c3 ), .G0(\全加器_g ), .G1(\全加器_2_g ), .G2(fa_1_g), .G3(\全加器_3_g ),
    .C2(\n4位先行进位部件clu_1_c2 ), .C4(Cout), .C0(Cin), .Pg(Pg), .Gg(Gg));
  FA fa_1 (.A(X[2]), .F(F[2]), .B(Y[2]), .P(fa_1_p), .Cin(\n4位先行进位部件clu_1_c2 ), .G(fa_1_g));
  Hex_Digit_Display hex_digit_display_3 (.value(F));  // open: dp
  FA \u_全加器_3  (.A(X[3]), .F(F[3]), .B(Y[3]), .P(\全加器_3_p ), .Cin(\n4位先行进位部件clu_1_c3 ), .G(\全加器_3_g ));

  // Other names for the same wires on the sheet: Z[3:0] = F

  // Notes on the sheet:
  //   四位快速加法器CLA
  //   +
  //   =
  //   输出
  //   输入
endmodule

// 16-CLA
module \_16位先行进位加法器  (
  input  C0,
  input  [15:0] X,
  input  [15:0] Y,
  output C16,
  output Pg,
  output Gg,
  output [15:0] S
);

  wire \_4位CLA_2_gg , \_4位CLA_2_pg , \_4位CLA_3_gg , \_4位CLA_3_pg , \_4位CLA_4_gg , \_4位CLA_4_pg , \_4位CLA_gg ,
       \_4位CLA_pg , \n4位先行进位部件clu_1_c1 , \n4位先行进位部件clu_1_c2 , \n4位先行进位部件clu_1_c3 ;

  \_4位快速加法器CLA  \_4位CLA  (
    .X(X[15:12]), .F(S[15:12]), .Y(Y[15:12]), .Pg(\_4位CLA_pg ), .Cin(\n4位先行进位部件clu_1_c3 ), .Gg(\_4位CLA_gg ));  // open: Cout
  \_4位快速加法器CLA  \_4位CLA_2  (
    .X(X[11:8]), .F(S[11:8]), .Y(Y[11:8]), .Pg(\_4位CLA_2_pg ), .Cin(\n4位先行进位部件clu_1_c2 ), .Gg(\_4位CLA_2_gg ));  // open: Cout
  \_4位先行进位部件CLU  \u_4位先行进位部件clu_1  (
    .P0(\_4位CLA_4_pg ), .P1(\_4位CLA_3_pg ), .P2(\_4位CLA_2_pg ), .P3(\_4位CLA_pg ), .C1(\n4位先行进位部件clu_1_c1 ),
    .C3(\n4位先行进位部件clu_1_c3 ), .G0(\_4位CLA_4_gg ), .G1(\_4位CLA_3_gg ), .G2(\_4位CLA_2_gg ), .G3(\_4位CLA_gg ),
    .C2(\n4位先行进位部件clu_1_c2 ), .C4(C16), .C0(C0), .Pg(Pg), .Gg(Gg));
  \_4位快速加法器CLA  \_4位CLA_3  (
    .X(X[7:4]), .F(S[7:4]), .Y(Y[7:4]), .Pg(\_4位CLA_3_pg ), .Cin(\n4位先行进位部件clu_1_c1 ), .Gg(\_4位CLA_3_gg ));  // open: Cout
  \_4位快速加法器CLA  \_4位CLA_4  (
    .X(X[3:0]), .F(S[3:0]), .Y(Y[3:0]), .Pg(\_4位CLA_4_pg ), .Cin(C0), .Gg(\_4位CLA_4_gg ));  // open: Cout
  // Probe on X
  // Probe on Y
  // Probe on S

  // Other names for the same wires on the sheet: S0[3:0] = S[3:0]; S1[3:0] = S[7:4]; S2[3:0] = S[11:8];
  //   S3[3:0] = S[15:12]

  // Notes on the sheet:
  //   Y: pull=down
  //   X: pull=down
  //   C0: pull=down
  //   16位快速加法器
  //   输入引脚区
  //   功能说明:16位Adder  S=X+Y，C16为最高位进位位，C0为进位输入， Pg、Gg为成组进位生成传递函数
  //   输出引脚区
  //   +
  //   =
  //   无符号加法
endmodule

// 加法器
module \_32位加法器  (
  input  [31:0] X,
  input  Cin,
  input  [31:0] Y,
  output OF,
  output CF,
  output [31:0] S,
  output ZF,
  output SF,
  output Cout
);

  wire and_1_out, and_2_out, \n16位先行进位加法器_2_c16 , not_1_out, not_2_out, not_3_out;
  wire [1:0] or_5_out;
  wire [3:0] or_4_out;
  wire [7:0] or_2_out;
  wire [15:0] or_1_out;

  \_16位先行进位加法器  \u_16位先行进位加法器_1  (
    .X(X[31:16]), .Y(Y[31:16]), .C0(\n16位先行进位加法器_2_c16 ), .S(S[31:16]), .C16(Cout));  // open: Pg, Gg
  not not_1 (not_1_out, X[31]);
  \_16位先行进位加法器  \u_16位先行进位加法器_2  (
    .X(X[15:0]), .Y(Y[15:0]), .C0(Cin), .S(S[15:0]), .C16(\n16位先行进位加法器_2_c16 ));  // open: Pg, Gg
  not not_2 (not_2_out, S[31]);
  assign or_1_out = S[15:0] | S[31:16];  // OR_Gate or_1, 16 bits wide
  not not_3 (not_3_out, Y[31]);
  assign or_2_out = or_1_out[7:0] | or_1_out[15:8];  // OR_Gate or_2, 8 bits wide
  and and_1 (and_1_out, Y[31], X[31], not_2_out);
  or or_3 (OF, and_1_out, and_2_out);
  and and_2 (and_2_out, not_3_out, not_1_out, S[31]);
  assign or_4_out = or_2_out[3:0] | or_2_out[7:4];  // OR_Gate or_4, 4 bits wide
  xor xor_1 (CF, Cin, Cout);
  // Probe on X
  // Probe on Y
  // Probe on S
  assign or_5_out = or_4_out[1:0] | or_4_out[3:2];  // OR_Gate or_5, 2 bits wide
  nor nor_1 (ZF, or_5_out[0], or_5_out[1]);

  assign SF = S[31];

  // Notes on the sheet:
  //   Cin: pull=down
  //   Y: pull=down
  //   X: pull=down
  //   带标志位的32位快速加法器
  //   输入引脚区
  //   输出引脚区
  //   功能说明:32位Adder  S=X+Y，Cout为最高位进位位，Cin为进位输入， S为和，OF、CF、ZF、SF为标志位。
  //   +
  //   =
  //   无符号加法
endmodule

// ALU操作控制信号
module \ALU操作控制信号生成部件  (
  input  [3:0] ALUctr,
  output SUBctr,
  output SFTctr,
  output SIGctr,
  output ALctr,
  output [2:0] OPctr
);

  subctr subctr_1 (.out_5(SUBctr), ._3(ALUctr[3]), ._2(ALUctr[2]), ._1(ALUctr[1]), ._0(ALUctr[0]));
  and and_1 (SIGctr, ~ALUctr[0], ALUctr[1], ~ALUctr[2], ~ALUctr[3]);  // AND_Gate
  and and_2 (SFTctr, ALUctr[0], ~ALUctr[1], ~ALUctr[2], ~ALUctr[3]);  // AND_Gate
  and and_3 (ALctr, ALUctr[0], ~ALUctr[1], ALUctr[2], ALUctr[3]);  // AND_Gate
  op0 op0_1 (.out_5(OPctr[0]), ._3(ALUctr[3]), ._2(ALUctr[2]), ._1(ALUctr[1]), ._0(ALUctr[0]));
  op1 op1_1 (.out_5(OPctr[1]), ._3(ALUctr[3]), ._2(ALUctr[2]), ._1(ALUctr[1]), ._0(ALUctr[0]));
  op2 op2_1 (.out_5(OPctr[2]), ._3(ALUctr[3]), ._2(ALUctr[2]), ._1(ALUctr[1]), ._0(ALUctr[0]));

  // Other names for the same wires on the sheet: LRctr = SFTctr

  // Notes on the sheet:
  //   输入引脚
  //   ALU操作控制信号生成部件
  //   输出引脚
endmodule

module ALU (
  input  [31:0] A,
  input  [31:0] B,
  input  [3:0] ALUctr,
  output [31:0] S,
  output Zero
);

  wire \alu操作控制信号生成部件_1_alctr , \alu操作控制信号生成部件_1_sftctr , \alu操作控制信号生成部件_1_sigctr , \alu操作控制信号生成部件_1_subctr ,
       multiplexer_1_out, \n32位加法器_1_cout , \n32位加法器_1_of , \n32位加法器_1_sf , xor_1_out, xor_2_out;
  wire [2:0] \alu操作控制信号生成部件_1_opctr ;
  wire [31:0] ands_1_out_3, bit_extender_1_out, bit_extender_2_out, \n32位加法器_1_s , \n32位桶形移位器_1_dataout ,
       ors_1_out_3, xors_1_out_3, xors_2_out_3;

  assign bit_extender_1_out = {{31{\alu操作控制信号生成部件_1_subctr }}, \alu操作控制信号生成部件_1_subctr };  // Bit_Extender bit_extender_1
  ORs ors_1 (.in_1(B), .in_2(A), .out_3(ors_1_out_3));
  ANDs ands_1 (.in_1(A), .in_2(B), .out_3(ands_1_out_3));
  XORs xors_1 (.in_1(A), .in_2(B), .out_3(xors_1_out_3));
  XORs xors_2 (.in_1(B), .in_2(bit_extender_1_out), .out_3(xors_2_out_3));
  \_32位桶形移位器  \u_32位桶形移位器_1  (
    .L_R(\alu操作控制信号生成部件_1_sftctr ), .shamt(B[4:0]), .DataIn(A), .DataOut(\n32位桶形移位器_1_dataout ),
    .A_L(\alu操作控制信号生成部件_1_alctr ));
  \_32位加法器  \u_32位加法器_1  (
    .Cin(\alu操作控制信号生成部件_1_subctr ), .Cout(\n32位加法器_1_cout ), .X(A), .Y(xors_2_out_3), .S(\n32位加法器_1_s ),
    .OF(\n32位加法器_1_of ), .ZF(Zero), .SF(\n32位加法器_1_sf ));  // open: CF
  xor xor_1 (xor_1_out, \alu操作控制信号生成部件_1_subctr , \n32位加法器_1_cout );
  Multiplexer #(.enable("false")) multiplexer_1 (
    .in0(xor_1_out), .in1(xor_2_out), .out(multiplexer_1_out), .sel(\alu操作控制信号生成部件_1_sigctr ));
  xor xor_2 (xor_2_out, \n32位加法器_1_of , \n32位加法器_1_sf );
  Multiplexer #(.select(3), .width(32), .enable("false")) multiplexer_2 (
    .in0(\n32位加法器_1_s ), .in1(ands_1_out_3), .in2(ors_1_out_3), .in3(xors_1_out_3),
    .in4(\n32位桶形移位器_1_dataout ), .in5(B), .in6(bit_extender_2_out), .out(S), .sel(\alu操作控制信号生成部件_1_opctr ));  // open: in7
  \ALU操作控制信号生成部件  \alu操作控制信号生成部件_1  (
    .ALUctr(ALUctr), .SUBctr(\alu操作控制信号生成部件_1_subctr ), .SFTctr(\alu操作控制信号生成部件_1_sftctr ),
    .SIGctr(\alu操作控制信号生成部件_1_sigctr ), .ALctr(\alu操作控制信号生成部件_1_alctr ), .OPctr(\alu操作控制信号生成部件_1_opctr ));
  assign bit_extender_2_out = {{31{1'b0}}, multiplexer_1_out};  // Bit_Extender bit_extender_2
  // Probe on A
  // Probe on B
  // Probe on S

  // Other names for the same wires on the sheet: Result[31:0] = S

  // Notes on the sheet:
  //   A: pull=down
  //   ALUctr: pull=down
  //   B: pull=down
  //   输入引脚区
  //   32位算术逻辑运算单元ALU
  //   功能说明:32位ALU，输入32位操作数A、B，4位控制信号ALUctr，输出32位结果Reseult和1位Zero标志位
  //   输出引脚区
  //   操作数和结果
endmodule

// 移位器
module \_32位桶形移位器  (
  input  L_R,
  input  [4:0] shamt,
  input  [31:0] DataIn,
  input  A_L,
  output [31:0] DataOut
);

  wire not_1_out;
  wire [0:0] not_2_out;
  wire [31:0] multiplexer_1_out, multiplexer_2_out, multiplexer_3_out, multiplexer_4_out, new_1_bit_1_out_3,
       new_1_bit_1_out_4, new_2_bit_1_out_3, new_2_bit_1_out_4, new_4_bit_1_out_3, new_4_bit_1_out_4,
       new_8_bit_1_out_3, new_8_bit_1_out_4, new_16_bit_1_out_3, new_16_bit_1_out_4;

  new_1_bit new_1_bit_1 (.in_1(DataIn), .out_3(new_1_bit_1_out_3), .out_4(new_1_bit_1_out_4), .A_L(not_1_out));
  not not_1 (not_1_out, A_L);
  not not_2 (not_2_out[0], L_R);
  Multiplexer #(.select(2), .width(32), .enable("false")) multiplexer_1 (
    .in0(DataIn), .in1(DataIn), .in2(new_1_bit_1_out_3), .in3(new_1_bit_1_out_4), .out(multiplexer_1_out),
    .sel({shamt[0], not_2_out[0]}));
  new_2_bit new_2_bit_1 (
    .in_1(multiplexer_1_out), .out_3(new_2_bit_1_out_3), .out_4(new_2_bit_1_out_4), .A_L(not_1_out));
  Multiplexer #(.select(2), .width(32), .enable("false")) multiplexer_2 (
    .in0(multiplexer_1_out), .in1(multiplexer_1_out), .in2(new_2_bit_1_out_3), .in3(new_2_bit_1_out_4),
    .out(multiplexer_2_out), .sel({shamt[1], not_2_out[0]}));
  new_4_bit new_4_bit_1 (
    .in_1(multiplexer_2_out), .out_3(new_4_bit_1_out_3), .out_4(new_4_bit_1_out_4), .A_L(not_1_out));
  Multiplexer #(.select(2), .width(32), .enable("false")) multiplexer_3 (
    .in0(multiplexer_2_out), .in1(multiplexer_2_out), .in2(new_4_bit_1_out_3), .in3(new_4_bit_1_out_4),
    .out(multiplexer_3_out), .sel({shamt[2], not_2_out[0]}));
  new_8_bit new_8_bit_1 (
    .in_1(multiplexer_3_out), .out_3(new_8_bit_1_out_3), .out_4(new_8_bit_1_out_4), .A_L(not_1_out));
  Multiplexer #(.select(2), .width(32), .enable("false")) multiplexer_4 (
    .in0(multiplexer_3_out), .in1(multiplexer_3_out), .in2(new_8_bit_1_out_3), .in3(new_8_bit_1_out_4),
    .out(multiplexer_4_out), .sel({shamt[3], not_2_out[0]}));
  new_16_bit new_16_bit_1 (
    .in_1(multiplexer_4_out), .out_3(new_16_bit_1_out_3), .out_4(new_16_bit_1_out_4), .A_L(not_1_out));
  Multiplexer #(.select(2), .width(32), .enable("false")) multiplexer_5 (
    .in0(multiplexer_4_out), .in1(multiplexer_4_out), .in2(new_16_bit_1_out_3), .in3(new_16_bit_1_out_4),
    .out(DataOut), .sel({shamt[4], not_2_out[0]}));

  // Other names for the same wires on the sheet: Arth_Logic = A_L; Din[31:0] = DataIn; Dout[31:0] = DataOut;
  //   Left_Right = L_R

  // Notes on the sheet:
  //   输入信号
  //   L/R=1左移；=0右移
  //   A/L=1算术右移；=0逻辑右移
  //   32位桶形移位器
  //   输出信号
endmodule

module subctr (
  input  _3,
  input  _2,
  input  _1,
  input  _0,
  output out_5
);

  wire and_1_out, and_2_out, and_3_out;

  and and_1 (and_1_out, ~_0, _1, ~_2, ~_3);  // AND_Gate
  and and_2 (and_2_out, _0, _1, ~_2, ~_3);  // AND_Gate
  and and_3 (and_3_out, ~_0, ~_1, ~_2, _3);  // AND_Gate
  or or_1 (out_5, and_1_out, and_2_out, and_3_out);
endmodule

module op0 (
  input  _3,
  input  _2,
  input  _1,
  input  _0,
  output out_5
);

  wire and_1_out, and_2_out, and_3_out;

  and and_1 (and_1_out, ~_0, ~_1, _2, ~_3);  // AND_Gate
  and and_2 (and_2_out, _0, _1, _2, ~_3);  // AND_Gate
  and and_3 (and_3_out, _0, _1, _2, _3);
  or or_1 (out_5, and_1_out, and_2_out, and_3_out);
endmodule

module op1 (
  input  _3,
  input  _2,
  input  _1,
  input  _0,
  output out_5
);

  wire and_1_out, and_2_out, and_3_out, and_4_out;

  and and_1 (and_1_out, ~_0, _1, ~_2, ~_3);  // AND_Gate
  and and_2 (and_2_out, _0, _1, ~_2, ~_3);  // AND_Gate
  and and_3 (and_3_out, ~_0, ~_1, _2, ~_3);  // AND_Gate
  and and_4 (and_4_out, ~_0, _1, _2, ~_3);  // AND_Gate
  or or_1 (out_5, and_1_out, and_2_out, and_3_out, and_4_out);
endmodule

module op2 (
  input  _3,
  input  _2,
  input  _1,
  input  _0,
  output out_5
);

  wire and_1_out, and_2_out, and_3_out, and_4_out, and_5_out, and_6_out;

  and and_1 (and_1_out, _0, ~_1, ~_2, ~_3);  // AND_Gate
  and and_2 (and_2_out, ~_0, _1, ~_2, ~_3);  // AND_Gate
  and and_3 (and_3_out, _0, _1, ~_2, ~_3);  // AND_Gate
  and and_4 (and_4_out, _0, ~_1, _2, ~_3);  // AND_Gate
  and and_5 (and_5_out, _0, ~_1, _2, _3);  // AND_Gate
  and and_6 (and_6_out, _0, _1, _2, _3);
  or or_1 (out_5, and_1_out, and_2_out, and_3_out, and_4_out, and_5_out, and_6_out);
endmodule

module \_32_bit一位  (
  input  [31:0] in_1,
  input  A_L,
  output [31:0] out_3,
  output [31:0] out_4
);

  Multiplexer #(.enable("false")) multiplexer_1 (.in0(1'b0), .in1(in_1[0]), .out(out_4[31]), .sel(A_L));
  Multiplexer #(.enable("false")) multiplexer_2 (.in0(1'b0), .in1(in_1[31]), .out(out_3[0]), .sel(A_L));

  assign out_3[31:1] = in_1[30:0];
  assign out_4[30:0] = in_1[31:1];

  // Other names for the same wires on the sheet: out_L[31:0] = {in_1[30:0], out_3[0]}; input[31:0] = in_1;
  //   out_R[31:0] = {out_4[31], in_1[31:1]}
endmodule

module \_32_bit二位  (
  input  [31:0] in_1,
  input  A_L,
  output [31:0] out_3,
  output [31:0] out_4
);

  Multiplexer #(.enable("false")) multiplexer_1 (.in0(1'b0), .in1(in_1[0]), .out(out_4[30]), .sel(A_L));
  Multiplexer #(.enable("false")) multiplexer_2 (.in0(1'b0), .in1(in_1[31]), .out(out_3[1]), .sel(A_L));
  Multiplexer #(.enable("false")) multiplexer_3 (.in0(1'b0), .in1(in_1[1]), .out(out_4[31]), .sel(A_L));
  Multiplexer #(.enable("false")) multiplexer_4 (.in0(1'b0), .in1(in_1[30]), .out(out_3[0]), .sel(A_L));

  assign out_3[31:2] = in_1[29:0];
  assign out_4[29:0] = in_1[31:2];

  // Other names for the same wires on the sheet: out_L[31:0] = {in_1[29:0], out_3[1:0]}; input[31:0] = in_1;
  //   out_R[31:0] = {out_4[31:30], in_1[31:2]}
endmodule

module \_32_bit四位  (
  input  [31:0] in_1,
  input  A_L,
  output [31:0] out_3,
  output [31:0] out_4
);

  Multiplexer #(.enable("false")) multiplexer_1 (.in0(1'b0), .in1(in_1[0]), .out(out_4[28]), .sel(A_L));
  Multiplexer #(.enable("false")) multiplexer_2 (.in0(1'b0), .in1(in_1[31]), .out(out_3[3]), .sel(A_L));
  Multiplexer #(.enable("false")) multiplexer_3 (.in0(1'b0), .in1(in_1[1]), .out(out_4[29]), .sel(A_L));
  Multiplexer #(.enable("false")) multiplexer_4 (.in0(1'b0), .in1(in_1[30]), .out(out_3[2]), .sel(A_L));
  Multiplexer #(.enable("false")) multiplexer_5 (.in0(1'b0), .in1(in_1[2]), .out(out_4[30]), .sel(A_L));
  Multiplexer #(.enable("false")) multiplexer_6 (.in0(1'b0), .in1(in_1[29]), .out(out_3[1]), .sel(A_L));
  Multiplexer #(.enable("false")) multiplexer_7 (.in0(1'b0), .in1(in_1[3]), .out(out_4[31]), .sel(A_L));
  Multiplexer #(.enable("false")) multiplexer_8 (.in0(1'b0), .in1(in_1[28]), .out(out_3[0]), .sel(A_L));

  assign out_3[31:4] = in_1[27:0];
  assign out_4[27:0] = in_1[31:4];

  // Other names for the same wires on the sheet: out_L[31:0] = {in_1[27:0], out_3[3:0]}; input[31:0] = in_1;
  //   out_R[31:0] = {out_4[31:28], in_1[31:4]}
endmodule

module \_32_bit八位  (
  input  [31:0] in_1,
  input  A_L,
  output [31:0] out_3,
  output [31:0] out_4
);

  wire [7:0] multiplexer_16_out;

  Multiplexer #(.enable("false")) multiplexer_1 (.in0(1'b0), .in1(in_1[31]), .out(multiplexer_16_out[7]), .sel(A_L));
  Multiplexer #(.enable("false")) multiplexer_2 (.in0(1'b0), .in1(in_1[0]), .out(out_4[24]), .sel(A_L));
  Multiplexer #(.enable("false")) multiplexer_3 (.in0(1'b0), .in1(in_1[1]), .out(out_4[25]), .sel(A_L));
  Multiplexer #(.enable("false")) multiplexer_4 (.in0(1'b0), .in1(in_1[30]), .out(multiplexer_16_out[6]), .sel(A_L));
  Multiplexer #(.enable("false")) multiplexer_5 (.in0(1'b0), .in1(in_1[2]), .out(out_4[26]), .sel(A_L));
  Multiplexer #(.enable("false")) multiplexer_6 (.in0(1'b0), .in1(in_1[29]), .out(multiplexer_16_out[5]), .sel(A_L));
  Multiplexer #(.enable("false")) multiplexer_7 (.in0(1'b0), .in1(in_1[3]), .out(out_4[27]), .sel(A_L));
  Multiplexer #(.enable("false")) multiplexer_8 (.in0(1'b0), .in1(in_1[4]), .out(out_4[28]), .sel(A_L));
  Multiplexer #(.enable("false")) multiplexer_9 (.in0(1'b0), .in1(in_1[28]), .out(multiplexer_16_out[4]), .sel(A_L));
  Multiplexer #(.enable("false")) multiplexer_10 (.in0(1'b0), .in1(in_1[5]), .out(out_4[29]), .sel(A_L));
  Multiplexer #(.enable("false")) multiplexer_11 (.in0(1'b0), .in1(in_1[27]), .out(multiplexer_16_out[3]), .sel(A_L));
  Multiplexer #(.enable("false")) multiplexer_12 (.in0(1'b0), .in1(in_1[6]), .out(out_4[30]), .sel(A_L));
  Multiplexer #(.enable("false")) multiplexer_13 (.in0(1'b0), .in1(in_1[26]), .out(multiplexer_16_out[2]), .sel(A_L));
  Multiplexer #(.enable("false")) multiplexer_14 (.in0(1'b0), .in1(in_1[25]), .out(multiplexer_16_out[1]), .sel(A_L));
  Multiplexer #(.enable("false")) multiplexer_15 (.in0(1'b0), .in1(in_1[7]), .out(out_4[31]), .sel(A_L));
  Multiplexer #(.enable("false")) multiplexer_16 (.in0(1'b0), .in1(in_1[24]), .out(multiplexer_16_out[0]), .sel(A_L));

  assign out_4[23:0] = in_1[31:8];

  // Other names for the same wires on the sheet: input[31:0] = in_1; out_L[31:0] = out_3;
  //   out_R[31:0] = {out_4[31:24], in_1[31:8]}
endmodule

module XORs (
  input  [31:0] in_1,
  input  [31:0] in_2,
  output [31:0] out_3
);

  xor xor_1 (out_3[0], in_1[0], in_2[0]);
  xor xor_2 (out_3[1], in_1[1], in_2[1]);
  xor xor_3 (out_3[2], in_1[2], in_2[2]);
  xor xor_4 (out_3[3], in_1[3], in_2[3]);
  xor xor_5 (out_3[4], in_1[4], in_2[4]);
  xor xor_6 (out_3[5], in_1[5], in_2[5]);
  xor xor_7 (out_3[6], in_1[6], in_2[6]);
  xor xor_8 (out_3[7], in_1[7], in_2[7]);
  xor xor_9 (out_3[8], in_1[8], in_2[8]);
  xor xor_10 (out_3[9], in_1[9], in_2[9]);
  xor xor_11 (out_3[10], in_1[10], in_2[10]);
  xor xor_12 (out_3[11], in_1[11], in_2[11]);
  xor xor_13 (out_3[12], in_1[12], in_2[12]);
  xor xor_14 (out_3[13], in_1[13], in_2[13]);
  xor xor_15 (out_3[14], in_1[14], in_2[14]);
  xor xor_16 (out_3[15], in_1[15], in_2[15]);
  xor xor_17 (out_3[16], in_1[16], in_2[16]);
  xor xor_18 (out_3[17], in_1[17], in_2[17]);
  xor xor_19 (out_3[18], in_1[18], in_2[18]);
  xor xor_20 (out_3[19], in_1[19], in_2[19]);
  xor xor_21 (out_3[20], in_1[20], in_2[20]);
  xor xor_22 (out_3[21], in_1[21], in_2[21]);
  xor xor_23 (out_3[22], in_1[22], in_2[22]);
  xor xor_24 (out_3[23], in_1[23], in_2[23]);
  xor xor_25 (out_3[24], in_1[24], in_2[24]);
  xor xor_26 (out_3[25], in_1[25], in_2[25]);
  xor xor_27 (out_3[26], in_1[26], in_2[26]);
  xor xor_28 (out_3[27], in_1[27], in_2[27]);
  xor xor_29 (out_3[28], in_1[28], in_2[28]);
  xor xor_30 (out_3[29], in_1[29], in_2[29]);
  xor xor_31 (out_3[30], in_1[30], in_2[30]);
  xor xor_32 (out_3[31], in_1[31], in_2[31]);

  // Other names for the same wires on the sheet: A[31:0] = in_1; B[31:0] = in_2; C[31:0] = out_3
endmodule

module \_32_bit十六位  (
  input  [31:0] in_1,
  input  A_L,
  output [31:0] out_3,
  output [31:0] out_4
);

  Multiplexer #(.enable("false")) multiplexer_1 (.in0(1'b0), .in1(in_1[31]), .out(out_3[15]), .sel(A_L));
  Multiplexer #(.enable("false")) multiplexer_2 (.in0(1'b0), .in1(in_1[0]), .out(out_4[16]), .sel(A_L));
  Multiplexer #(.enable("false")) multiplexer_3 (.in0(1'b0), .in1(in_1[30]), .out(out_3[14]), .sel(A_L));
  Multiplexer #(.enable("false")) multiplexer_4 (.in0(1'b0), .in1(in_1[1]), .out(out_4[17]), .sel(A_L));
  Multiplexer #(.enable("false")) multiplexer_5 (.in0(1'b0), .in1(in_1[29]), .out(out_3[13]), .sel(A_L));
  Multiplexer #(.enable("false")) multiplexer_6 (.in0(1'b0), .in1(in_1[2]), .out(out_4[18]), .sel(A_L));
  Multiplexer #(.enable("false")) multiplexer_7 (.in0(1'b0), .in1(in_1[3]), .out(out_4[19]), .sel(A_L));
  Multiplexer #(.enable("false")) multiplexer_8 (.in0(1'b0), .in1(in_1[15]), .out(out_4[31]), .sel(A_L));
  Multiplexer #(.enable("false")) multiplexer_9 (.in0(1'b0), .in1(in_1[28]), .out(out_3[12]), .sel(A_L));
  Multiplexer #(.enable("false")) multiplexer_10 (.in0(1'b0), .in1(in_1[4]), .out(out_4[20]), .sel(A_L));
  Multiplexer #(.enable("false")) multiplexer_11 (.in0(1'b0), .in1(in_1[27]), .out(out_3[11]), .sel(A_L));
  Multiplexer #(.enable("false")) multiplexer_12 (.in0(1'b0), .in1(in_1[5]), .out(out_4[21]), .sel(A_L));
  Multiplexer #(.enable("false")) multiplexer_13 (.in0(1'b0), .in1(in_1[26]), .out(out_3[10]), .sel(A_L));
  Multiplexer #(.enable("false")) multiplexer_14 (.in0(1'b0), .in1(in_1[25]), .out(out_3[9]), .sel(A_L));
  Multiplexer #(.enable("false")) multiplexer_15 (.in0(1'b0), .in1(in_1[6]), .out(out_4[22]), .sel(A_L));
  Multiplexer #(.enable("false")) multiplexer_16 (.in0(1'b0), .in1(in_1[24]), .out(out_3[8]), .sel(A_L));
  Multiplexer #(.enable("false")) multiplexer_17 (.in0(1'b0), .in1(in_1[7]), .out(out_4[23]), .sel(A_L));
  Multiplexer #(.enable("false")) multiplexer_18 (.in0(1'b0), .in1(in_1[23]), .out(out_3[7]), .sel(A_L));
  Multiplexer #(.enable("false")) multiplexer_19 (.in0(1'b0), .in1(in_1[8]), .out(out_4[24]), .sel(A_L));
  Multiplexer #(.enable("false")) multiplexer_20 (.in0(1'b0), .in1(in_1[22]), .out(out_3[6]), .sel(A_L));
  Multiplexer #(.enable("false")) multiplexer_21 (.in0(1'b0), .in1(in_1[9]), .out(out_4[25]), .sel(A_L));
  Multiplexer #(.enable("false")) multiplexer_22 (.in0(1'b0), .in1(in_1[21]), .out(out_3[5]), .sel(A_L));
  Multiplexer #(.enable("false")) multiplexer_23 (.in0(1'b0), .in1(in_1[20]), .out(out_3[4]), .sel(A_L));
  Multiplexer #(.enable("false")) multiplexer_24 (.in0(1'b0), .in1(in_1[10]), .out(out_4[26]), .sel(A_L));
  Multiplexer #(.enable("false")) multiplexer_25 (.in0(1'b0), .in1(in_1[19]), .out(out_3[3]), .sel(A_L));
  Multiplexer #(.enable("false")) multiplexer_26 (.in0(1'b0), .in1(in_1[11]), .out(out_4[27]), .sel(A_L));
  Multiplexer #(.enable("false")) multiplexer_27 (.in0(1'b0), .in1(in_1[18]), .out(out_3[2]), .sel(A_L));
  Multiplexer #(.enable("false")) multiplexer_28 (.in0(1'b0), .in1(in_1[12]), .out(out_4[28]), .sel(A_L));
  Multiplexer #(.enable("false")) multiplexer_29 (.in0(1'b0), .in1(in_1[17]), .out(out_3[1]), .sel(A_L));
  Multiplexer #(.enable("false")) multiplexer_30 (.in0(1'b0), .in1(in_1[13]), .out(out_4[29]), .sel(A_L));
  Multiplexer #(.enable("false")) multiplexer_31 (.in0(1'b0), .in1(in_1[16]), .out(out_3[0]), .sel(A_L));
  Multiplexer #(.enable("false")) multiplexer_32 (.in0(1'b0), .in1(in_1[14]), .out(out_4[30]), .sel(A_L));

  assign out_3[31:16] = in_1[15:0];
  assign out_4[15:0] = in_1[31:16];

  // Other names for the same wires on the sheet: out_L[31:0] = {in_1[15:0], out_3[15:0]}; input[31:0] = in_1;
  //   out_R[31:0] = {out_4[31:16], in_1[31:16]}
endmodule

module ORs (
  input  [31:0] in_1,
  input  [31:0] in_2,
  output [31:0] out_3
);

  or or_1 (out_3[0], in_1[0], in_2[0]);
  or or_2 (out_3[1], in_1[1], in_2[1]);
  or or_3 (out_3[2], in_1[2], in_2[2]);
  or or_4 (out_3[3], in_1[3], in_2[3]);
  or or_5 (out_3[4], in_1[4], in_2[4]);
  or or_6 (out_3[5], in_1[5], in_2[5]);
  or or_7 (out_3[6], in_1[6], in_2[6]);
  or or_8 (out_3[7], in_1[7], in_2[7]);
  or or_9 (out_3[8], in_1[8], in_2[8]);
  or or_10 (out_3[9], in_1[9], in_2[9]);
  or or_11 (out_3[10], in_1[10], in_2[10]);
  or or_12 (out_3[11], in_1[11], in_2[11]);
  or or_13 (out_3[12], in_1[12], in_2[12]);
  or or_14 (out_3[13], in_1[13], in_2[13]);
  or or_15 (out_3[14], in_1[14], in_2[14]);
  or or_16 (out_3[15], in_1[15], in_2[15]);
  or or_17 (out_3[16], in_1[16], in_2[16]);
  or or_18 (out_3[17], in_1[17], in_2[17]);
  or or_19 (out_3[18], in_1[18], in_2[18]);
  or or_20 (out_3[19], in_1[19], in_2[19]);
  or or_21 (out_3[20], in_1[20], in_2[20]);
  or or_22 (out_3[21], in_1[21], in_2[21]);
  or or_23 (out_3[22], in_1[22], in_2[22]);
  or or_24 (out_3[23], in_1[23], in_2[23]);
  or or_25 (out_3[24], in_1[24], in_2[24]);
  or or_26 (out_3[25], in_1[25], in_2[25]);
  or or_27 (out_3[26], in_1[26], in_2[26]);
  or or_28 (out_3[27], in_1[27], in_2[27]);
  or or_29 (out_3[28], in_1[28], in_2[28]);
  or or_30 (out_3[29], in_1[29], in_2[29]);
  or or_31 (out_3[30], in_1[30], in_2[30]);
  or or_32 (out_3[31], in_1[31], in_2[31]);

  // Other names for the same wires on the sheet: A[31:0] = in_1; B[31:0] = in_2; C[31:0] = out_3
endmodule

module ANDs (
  input  [31:0] in_1,
  input  [31:0] in_2,
  output [31:0] out_3
);

  and and_1 (out_3[0], in_1[0], in_2[0]);
  and and_2 (out_3[1], in_1[1], in_2[1]);
  and and_3 (out_3[2], in_1[2], in_2[2]);
  and and_4 (out_3[3], in_1[3], in_2[3]);
  and and_5 (out_3[4], in_1[4], in_2[4]);
  and and_6 (out_3[5], in_1[5], in_2[5]);
  and and_7 (out_3[6], in_1[6], in_2[6]);
  and and_8 (out_3[7], in_1[7], in_2[7]);
  and and_9 (out_3[8], in_1[8], in_2[8]);
  and and_10 (out_3[9], in_1[9], in_2[9]);
  and and_11 (out_3[10], in_1[10], in_2[10]);
  and and_12 (out_3[11], in_1[11], in_2[11]);
  and and_13 (out_3[12], in_1[12], in_2[12]);
  and and_14 (out_3[13], in_1[13], in_2[13]);
  and and_15 (out_3[14], in_1[14], in_2[14]);
  and and_16 (out_3[15], in_1[15], in_2[15]);
  and and_17 (out_3[16], in_1[16], in_2[16]);
  and and_18 (out_3[17], in_1[17], in_2[17]);
  and and_19 (out_3[18], in_1[18], in_2[18]);
  and and_20 (out_3[19], in_1[19], in_2[19]);
  and and_21 (out_3[20], in_1[20], in_2[20]);
  and and_22 (out_3[21], in_1[21], in_2[21]);
  and and_23 (out_3[22], in_1[22], in_2[22]);
  and and_24 (out_3[23], in_1[23], in_2[23]);
  and and_25 (out_3[24], in_1[24], in_2[24]);
  and and_26 (out_3[25], in_1[25], in_2[25]);
  and and_27 (out_3[26], in_1[26], in_2[26]);
  and and_28 (out_3[27], in_1[27], in_2[27]);
  and and_29 (out_3[28], in_1[28], in_2[28]);
  and and_30 (out_3[29], in_1[29], in_2[29]);
  and and_31 (out_3[30], in_1[30], in_2[30]);
  and and_32 (out_3[31], in_1[31], in_2[31]);

  // Other names for the same wires on the sheet: A[31:0] = in_1; B[31:0] = in_2; C[31:0] = out_3
endmodule

module new_1_bit (
  input  [31:0] in_1,
  input  A_L,
  output [31:0] out_3,
  output [31:0] out_4
);

  Multiplexer #(.enable("false")) multiplexer_1 (.in0(in_1[31]), .in1(1'b0), .out(out_4[31]), .sel(A_L));
  Multiplexer #(.enable("false")) multiplexer_2 (.in0(in_1[31]), .in1(1'b0), .out(out_3[0]), .sel(A_L));

  assign out_3[31:1] = in_1[30:0];
  assign out_4[30:0] = in_1[31:1];

  // Other names for the same wires on the sheet: out_L[31:0] = {in_1[30:0], out_3[0]}; input[31:0] = in_1;
  //   out_R[31:0] = {out_4[31], in_1[31:1]}
endmodule

module new_2_bit (
  input  [31:0] in_1,
  input  A_L,
  output [31:0] out_3,
  output [31:0] out_4
);

  wire not_1_out, not_2_out;

  not not_1 (not_1_out, A_L);
  not not_2 (not_2_out, A_L);
  Multiplexer #(.enable("false")) multiplexer_1 (.in0(1'b0), .in1(in_1[31]), .out(out_4[30]), .sel(not_2_out));
  Multiplexer #(.enable("false")) multiplexer_2 (.in0(1'b0), .in1(in_1[31]), .out(out_3[1]), .sel(not_1_out));
  Multiplexer #(.enable("false")) multiplexer_3 (.in0(1'b0), .in1(in_1[31]), .out(out_4[31]), .sel(not_2_out));
  Multiplexer #(.enable("false")) multiplexer_4 (.in0(1'b0), .in1(in_1[31]), .out(out_3[0]), .sel(not_1_out));

  assign out_3[31:2] = in_1[29:0];
  assign out_4[29:0] = in_1[31:2];

  // Other names for the same wires on the sheet: out_L[31:0] = {in_1[29:0], out_3[1:0]}; input[31:0] = in_1;
  //   out_R[31:0] = {out_4[31:30], in_1[31:2]}
endmodule

module new_4_bit (
  input  [31:0] in_1,
  input  A_L,
  output [31:0] out_3,
  output [31:0] out_4
);

  wire not_1_out, not_2_out;

  not not_1 (not_1_out, A_L);
  Multiplexer #(.enable("false")) multiplexer_1 (.in0(1'b0), .in1(in_1[31]), .out(out_4[28]), .sel(not_2_out));
  not not_2 (not_2_out, A_L);
  Multiplexer #(.enable("false")) multiplexer_2 (.in0(1'b0), .in1(in_1[31]), .out(out_3[3]), .sel(not_1_out));
  Multiplexer #(.enable("false")) multiplexer_3 (.in0(1'b0), .in1(in_1[31]), .out(out_4[29]), .sel(not_2_out));
  Multiplexer #(.enable("false")) multiplexer_4 (.in0(1'b0), .in1(in_1[31]), .out(out_3[2]), .sel(not_1_out));
  Multiplexer #(.enable("false")) multiplexer_5 (.in0(1'b0), .in1(in_1[31]), .out(out_4[30]), .sel(not_2_out));
  Multiplexer #(.enable("false")) multiplexer_6 (.in0(1'b0), .in1(in_1[31]), .out(out_3[1]), .sel(not_1_out));
  Multiplexer #(.enable("false")) multiplexer_7 (.in0(1'b0), .in1(in_1[31]), .out(out_4[31]), .sel(not_2_out));
  Multiplexer #(.enable("false")) multiplexer_8 (.in0(1'b0), .out(out_3[0]), .sel(not_1_out));  // open: in1

  assign out_3[31:4] = in_1[27:0];
  assign out_4[27:0] = in_1[31:4];

  // Other names for the same wires on the sheet: out_L[31:0] = {in_1[27:0], out_3[3:0]}; input[31:0] = in_1;
  //   out_R[31:0] = {out_4[31:28], in_1[31:4]}
endmodule

module new_8_bit (
  input  [31:0] in_1,
  input  A_L,
  output [31:0] out_3,
  output [31:0] out_4
);

  wire not_1_out, not_2_out;
  wire [7:0] multiplexer_16_out;

  not not_1 (not_1_out, A_L);
  not not_2 (not_2_out, A_L);
  Multiplexer #(.enable("false")) multiplexer_1 (
    .in0(1'b0), .in1(in_1[31]), .out(multiplexer_16_out[7]), .sel(not_1_out));
  Multiplexer #(.enable("false")) multiplexer_2 (.in0(1'b0), .in1(in_1[31]), .out(out_4[24]), .sel(not_2_out));
  Multiplexer #(.enable("false")) multiplexer_3 (.in0(1'b0), .in1(in_1[31]), .out(out_4[25]), .sel(not_2_out));
  Multiplexer #(.enable("false")) multiplexer_4 (
    .in0(1'b0), .in1(in_1[31]), .out(multiplexer_16_out[6]), .sel(not_1_out));
  Multiplexer #(.enable("false")) multiplexer_5 (.in0(1'b0), .in1(in_1[31]), .out(out_4[26]), .sel(not_2_out));
  Multiplexer #(.enable("false")) multiplexer_6 (
    .in0(1'b0), .in1(in_1[31]), .out(multiplexer_16_out[5]), .sel(not_1_out));
  Multiplexer #(.enable("false")) multiplexer_7 (.in0(1'b0), .in1(in_1[31]), .out(out_4[27]), .sel(not_2_out));
  Multiplexer #(.enable("false")) multiplexer_8 (.in0(1'b0), .in1(in_1[31]), .out(out_4[28]), .sel(not_2_out));
  Multiplexer #(.enable("false")) multiplexer_9 (
    .in0(1'b0), .in1(in_1[31]), .out(multiplexer_16_out[4]), .sel(not_1_out));
  Multiplexer #(.enable("false")) multiplexer_10 (.in0(1'b0), .in1(in_1[31]), .out(out_4[29]), .sel(not_2_out));
  Multiplexer #(.enable("false")) multiplexer_11 (
    .in0(1'b0), .in1(in_1[31]), .out(multiplexer_16_out[3]), .sel(not_1_out));
  Multiplexer #(.enable("false")) multiplexer_12 (.in0(1'b0), .in1(in_1[31]), .out(out_4[30]), .sel(not_2_out));
  Multiplexer #(.enable("false")) multiplexer_13 (
    .in0(1'b0), .in1(in_1[31]), .out(multiplexer_16_out[2]), .sel(not_1_out));
  Multiplexer #(.enable("false")) multiplexer_14 (
    .in0(1'b0), .in1(in_1[31]), .out(multiplexer_16_out[1]), .sel(not_1_out));
  Multiplexer #(.enable("false")) multiplexer_15 (.in0(1'b0), .in1(in_1[31]), .out(out_4[31]), .sel(not_2_out));
  Multiplexer #(.enable("false")) multiplexer_16 (
    .in0(1'b0), .in1(in_1[31]), .out(multiplexer_16_out[0]), .sel(not_1_out));

  assign out_4[23:0] = in_1[31:8];

  // Other names for the same wires on the sheet: input[31:0] = in_1; out_L[31:0] = out_3;
  //   out_R[31:0] = {out_4[31:24], in_1[31:8]}
endmodule

module new_16_bit (
  input  [31:0] in_1,
  input  A_L,
  output [31:0] out_3,
  output [31:0] out_4
);

  wire not_1_out, not_2_out;

  not not_1 (not_1_out, A_L);
  not not_2 (not_2_out, A_L);
  Multiplexer #(.enable("false")) multiplexer_1 (.in0(1'b0), .in1(in_1[31]), .out(out_3[15]), .sel(not_1_out));
  Multiplexer #(.enable("false")) multiplexer_2 (.in0(1'b0), .in1(in_1[31]), .out(out_4[16]), .sel(not_2_out));
  Multiplexer #(.enable("false")) multiplexer_3 (.in0(1'b0), .in1(in_1[31]), .out(out_3[14]), .sel(not_1_out));
  Multiplexer #(.enable("false")) multiplexer_4 (.in0(1'b0), .in1(in_1[31]), .out(out_4[17]), .sel(not_2_out));
  Multiplexer #(.enable("false")) multiplexer_5 (.in0(1'b0), .in1(in_1[31]), .out(out_3[13]), .sel(not_1_out));
  Multiplexer #(.enable("false")) multiplexer_6 (.in0(1'b0), .in1(in_1[31]), .out(out_4[18]), .sel(not_2_out));
  Multiplexer #(.enable("false")) multiplexer_7 (.in0(1'b0), .in1(in_1[31]), .out(out_4[19]), .sel(not_2_out));
  Multiplexer #(.enable("false")) multiplexer_8 (.in0(1'b0), .in1(in_1[31]), .out(out_4[31]), .sel(not_2_out));
  Multiplexer #(.enable("false")) multiplexer_9 (.in0(1'b0), .in1(in_1[31]), .out(out_3[12]), .sel(not_1_out));
  Multiplexer #(.enable("false")) multiplexer_10 (.in0(1'b0), .in1(in_1[31]), .out(out_4[20]), .sel(not_2_out));
  Multiplexer #(.enable("false")) multiplexer_11 (.in0(1'b0), .in1(in_1[31]), .out(out_3[11]), .sel(not_1_out));
  Multiplexer #(.enable("false")) multiplexer_12 (.in0(1'b0), .in1(in_1[31]), .out(out_4[21]), .sel(not_2_out));
  Multiplexer #(.enable("false")) multiplexer_13 (.in0(1'b0), .in1(in_1[31]), .out(out_3[10]), .sel(not_1_out));
  Multiplexer #(.enable("false")) multiplexer_14 (.in0(1'b0), .in1(in_1[31]), .out(out_3[9]), .sel(not_1_out));
  Multiplexer #(.enable("false")) multiplexer_15 (.in0(1'b0), .in1(in_1[31]), .out(out_4[22]), .sel(not_2_out));
  Multiplexer #(.enable("false")) multiplexer_16 (.in0(1'b0), .in1(in_1[31]), .out(out_3[8]), .sel(not_1_out));
  Multiplexer #(.enable("false")) multiplexer_17 (.in0(1'b0), .in1(in_1[31]), .out(out_4[23]), .sel(not_2_out));
  Multiplexer #(.enable("false")) multiplexer_18 (.in0(1'b0), .in1(in_1[31]), .out(out_3[7]), .sel(not_1_out));
  Multiplexer #(.enable("false")) multiplexer_19 (.in0(1'b0), .in1(in_1[31]), .out(out_4[24]), .sel(not_2_out));
  Multiplexer #(.enable("false")) multiplexer_20 (.in0(1'b0), .in1(in_1[31]), .out(out_3[6]), .sel(not_1_out));
  Multiplexer #(.enable("false")) multiplexer_21 (.in0(1'b0), .in1(in_1[31]), .out(out_4[25]), .sel(not_2_out));
  Multiplexer #(.enable("false")) multiplexer_22 (.in0(1'b0), .in1(in_1[31]), .out(out_3[5]), .sel(not_1_out));
  Multiplexer #(.enable("false")) multiplexer_23 (.in0(1'b0), .in1(in_1[31]), .out(out_3[4]), .sel(not_1_out));
  Multiplexer #(.enable("false")) multiplexer_24 (.in0(1'b0), .in1(in_1[31]), .out(out_4[26]), .sel(not_2_out));
  Multiplexer #(.enable("false")) multiplexer_25 (.in0(1'b0), .in1(in_1[31]), .out(out_3[3]), .sel(not_1_out));
  Multiplexer #(.enable("false")) multiplexer_26 (.in0(1'b0), .in1(in_1[31]), .out(out_4[27]), .sel(not_2_out));
  Multiplexer #(.enable("false")) multiplexer_27 (.in0(1'b0), .in1(in_1[31]), .out(out_3[2]), .sel(not_1_out));
  Multiplexer #(.enable("false")) multiplexer_28 (.in0(1'b0), .in1(in_1[31]), .out(out_4[28]), .sel(not_2_out));
  Multiplexer #(.enable("false")) multiplexer_29 (.in0(1'b0), .in1(in_1[31]), .out(out_3[1]), .sel(not_1_out));
  Multiplexer #(.enable("false")) multiplexer_30 (.in0(1'b0), .in1(in_1[31]), .out(out_4[29]), .sel(not_2_out));
  Multiplexer #(.enable("false")) multiplexer_31 (.in0(1'b0), .in1(in_1[31]), .out(out_3[0]), .sel(not_1_out));
  Multiplexer #(.enable("false")) multiplexer_32 (.in0(1'b0), .in1(in_1[31]), .out(out_4[30]), .sel(not_2_out));

  assign out_3[31:16] = in_1[15:0];
  assign out_4[15:0] = in_1[31:16];

  // Other names for the same wires on the sheet: out_L[31:0] = {in_1[15:0], out_3[15:0]}; input[31:0] = in_1;
  //   out_R[31:0] = {out_4[31:16], in_1[31:16]}
endmodule
